// Logisim project hack-computer.circ as structural Verilog: 5 circuits, main circuit alu
module alu (
  input  [15:0] x,
  input  zx,
  input  nx,
  input  [15:0] y,
  input  zy,
  input  ny,
  input  f,
  input  no,
  output [15:0] out,
  output zr,
  output ng
);

  wire [15:0] adder_1_out, and_1_out, multiplexer_1_out, multiplexer_2_out, multiplexer_3_out,
       multiplexer_4_out, multiplexer_5_out, not_1_out, not_2_out, not_3_out;

  Multiplexer #(.select(1), .width(16)) multiplexer_1 (.in0(x), .in1({16{1'b0}}), .out(multiplexer_1_out), .sel(zx));
  Multiplexer #(.select(1), .width(16)) multiplexer_2 (.in0(y), .in1({16{1'b0}}), .out(multiplexer_2_out), .sel(zy));
  assign not_1_out = ~multiplexer_1_out;  // NOT_Gate not_1, 16 bits wide
  assign not_2_out = ~multiplexer_2_out;  // NOT_Gate not_2, 16 bits wide
  Multiplexer #(.select(1), .width(16)) multiplexer_3 (
    .in0(multiplexer_1_out), .in1(not_1_out), .out(multiplexer_3_out), .sel(nx));
  Multiplexer #(.select(1), .width(16)) multiplexer_4 (
    .in0(multiplexer_2_out), .in1(not_2_out), .out(multiplexer_4_out), .sel(ny));
  assign and_1_out = multiplexer_3_out & multiplexer_4_out;  // AND_Gate and_1, 16 bits wide
  Adder #(.width(16)) adder_1 (
    .a(multiplexer_3_out), .b(multiplexer_4_out), .out(adder_1_out), .cin(1'b0));  // open: cout
  Multiplexer #(.select(1), .width(16)) multiplexer_5 (
    .in0(and_1_out), .in1(adder_1_out), .out(multiplexer_5_out), .sel(f));
  assign not_3_out = ~multiplexer_5_out;  // NOT_Gate not_3, 16 bits wide
  Multiplexer #(.select(1), .width(16)) multiplexer_6 (
    .in0(multiplexer_5_out), .in1(not_3_out), .out({ng, out[14:0]}), .sel(no));
  Comparator #(.width(16), .mode("unsigned")) comparator_1 (
    .a({16{1'b0}}), .b({ng, out[14:0]}), .eq(zr));  // open: gt, lt

  assign out[15] = ng;
endmodule

module register16 (
  input  [15:0] in,
  input  load,
  input  clock,
  output [15:0] out
);

  wire [15:0] multiplexer_1_out;

  Multiplexer #(.select(1), .width(16)) multiplexer_1 (.in0(out), .in1(in), .out(multiplexer_1_out), .sel(load));
  Register #(.width(16), .trigger("rising")) register_1 (.D(multiplexer_1_out), .Q(out), .clk(clock));  // open: en, clr
endmodule

module pc (
  input  [15:0] in,
  input  reset,
  input  load,
  input  inc,
  input  clock,
  output [15:0] out
);

  wire and_1_out, and_2_out, not_1_out, not_2_out;
  wire [15:0] adder_1_out, controlled_buffer_1_out;

  not not_1 (not_1_out, reset);
  not not_2 (not_2_out, load);
  and and_1 (and_1_out, not_1_out, load);
  and and_2 (and_2_out, not_1_out, not_2_out, inc);
  assign controlled_buffer_1_out = and_1_out ? in : 16'bz;  // Controlled_Buffer controlled_buffer_1
  assign controlled_buffer_1_out = and_2_out ? adder_1_out : 16'bz;  // Controlled_Buffer controlled_buffer_2
  Register #(.width(16), .trigger("rising")) register_1 (
    .D(controlled_buffer_1_out), .Q(out), .clk(clock), .clr(reset));  // open: en
  Adder #(.width(16)) adder_1 (.a(16'h1), .b(out), .out(adder_1_out), .cin(1'b0));  // open: cout
endmodule

module cpu (
  input  [15:0] in_data_mem,
  input  [15:0] instruction,
  input  clock,
  input  reset,
  output write_data_mem,
  output [15:0] ALU_out,
  output [15:0] data_mem,
  output [15:0] PC
);

  wire alu_1_ng, alu_1_zr, and_1_out, and_2_out, and_3_out, and_4_out, and_5_out, and_6_out, not_1_out,
       not_2_out, not_3_out, or_1_out, or_2_out;
  wire [15:0] multiplexer_1_out, multiplexer_2_out, register16_1_out;

  or or_1 (or_1_out, not_1_out, instruction[5]);
  Multiplexer #(.select(1), .width(16)) multiplexer_1 (
    .in0(ALU_out), .in1(instruction), .out(multiplexer_1_out), .sel(not_1_out));
  not not_1 (not_1_out, instruction[15]);
  and and_1 (and_1_out, instruction[2], alu_1_ng);
  and and_2 (and_2_out, instruction[1], alu_1_zr);
  and and_3 (and_3_out, instruction[0], and_6_out);
  and and_4 (and_4_out, instruction[15], instruction[4]);
  register16 register16_1 (.in(ALU_out), .load(and_4_out), .clock(clock), .out(register16_1_out));
  register16 register16_2 (.in(multiplexer_1_out), .load(or_1_out), .clock(clock), .out(data_mem));
  and and_5 (and_5_out, instruction[15], or_2_out);
  or or_2 (or_2_out, and_1_out, and_2_out, and_3_out);
  Multiplexer #(.select(1), .width(16)) multiplexer_2 (
    .in0(data_mem), .in1(in_data_mem), .out(multiplexer_2_out), .sel(instruction[12]));
  alu alu_1 (
    .x(register16_1_out), .zx(instruction[11]), .nx(instruction[10]), .y(multiplexer_2_out),
    .zy(instruction[9]), .ny(instruction[8]), .f(instruction[7]), .no(instruction[6]), .out(ALU_out),
    .zr(alu_1_zr), .ng(alu_1_ng));
  pc pc_1 (.in(data_mem), .reset(reset), .load(and_5_out), .inc(1'b1), .clock(clock), .out(PC));
  not not_2 (not_2_out, alu_1_ng);
  and and_6 (and_6_out, not_2_out, not_3_out);
  not not_3 (not_3_out, alu_1_zr);
  and and_7 (write_data_mem, instruction[15], instruction[3]);

  // Notes on the sheet:
  //   bit15
  //   bit0
  //   D
  //   A
  //   < 0
  //   = 0
  //   > 0
  //   ALU
  //   PC
endmodule

module hack_computer (
  input  reset
);

  wire and_1_out, and_2_out, and_3_out, clock_out, comparator_1_eq, comparator_2_eq, comparator_3_eq,
       comparator_4_gt, cpu_1_write_data_mem, not_1_out, not_2_out, not_3_out;
  wire [0:0] keyboard_1_avail;
  wire [6:0] keyboard_1_data;
  wire [15:0] controlled_buffer_1_out, cpu_1_alu_out, cpu_1_data_mem, cpu_1_pc, rom_1_data;

  ROM #(.addrWidth(16), .dataWidth(16)) rom_1 (.addr(cpu_1_pc), .data(rom_1_data), .sel(1'b1));
  Clock #(.highDuration(1), .lowDuration(1)) clock (.out(clock_out));
  cpu cpu_1 (
    .instruction(rom_1_data), .PC(cpu_1_pc), .clock(clock_out), .reset(reset),
    .write_data_mem(cpu_1_write_data_mem), .ALU_out(cpu_1_alu_out), .data_mem(cpu_1_data_mem),
    .in_data_mem(controlled_buffer_1_out));
  Comparator #(.width(16), .mode("unsigned")) comparator_1 (
    .a(cpu_1_data_mem), .b({16{1'b0}}), .eq(comparator_1_eq));  // open: gt, lt
  Comparator #(.width(16), .mode("unsigned")) comparator_2 (
    .a(cpu_1_data_mem), .b(16'h1), .eq(comparator_2_eq));  // open: gt, lt
  Comparator #(.width(16), .mode("unsigned")) comparator_3 (
    .a(cpu_1_data_mem), .b(16'h2), .eq(comparator_3_eq));  // open: gt, lt
  assign controlled_buffer_1_out = cpu_1_write_data_mem ? cpu_1_alu_out : 16'bz;  // Controlled_Buffer controlled_buffer_1
  not not_1 (not_1_out, cpu_1_write_data_mem);
  Comparator #(.width(16), .mode("unsigned")) comparator_4 (
    .a(cpu_1_data_mem), .b(16'h2), .gt(comparator_4_gt));  // open: eq, lt
  not not_2 (not_2_out, cpu_1_write_data_mem);
  not not_3 (not_3_out, cpu_1_write_data_mem);
  TTY #(.rows(8), .cols(32), .trigger("rising")) tty_1 (
    .data(cpu_1_alu_out[6:0]), .clk(clock_out), .we(and_1_out), .clr(reset));
  and and_1 (and_1_out, comparator_1_eq, cpu_1_write_data_mem);
  Keyboard #(.buflen(32), .trigger("rising")) keyboard_1 (
    .clk(clock_out), .re(and_2_out), .clr(reset), .avail(keyboard_1_avail[0]), .data(keyboard_1_data));
  and and_2 (and_2_out, comparator_2_eq, not_2_out);
  and and_3 (and_3_out, comparator_3_eq, not_3_out);
  RAM #(.addrWidth(16), .dataWidth(16), .bus("combined")) ram_1 (
    .addr(cpu_1_data_mem), .data(controlled_buffer_1_out), .sel(comparator_4_gt), .clk(clock_out),
    .ld(not_1_out), .clr(reset));
  assign controlled_buffer_1_out = and_3_out ? {{15{1'b0}}, keyboard_1_avail[0]} : 16'bz;  // Controlled_Buffer controlled_buffer_2
  assign controlled_buffer_1_out = and_2_out ? {{9{1'b0}}, keyboard_1_data} : 16'bz;  // Controlled_Buffer controlled_buffer_3

  // Notes on the sheet:
  //   instruction memory
  //   contents of rom_1 (hex, n*v repeats v):
  //   c 8c10 0 8308 4b 8c10 0 8308 45 8c10 0 8308 59 8c10 0 8308 3a 8c10 0 8308 2 9c10 14 8302 1 9c10 3
  //   8308 a 8c10 0 8308 3 9c10 0 8308 3 8388 20 84d0 0 8306 1c 8a87
  //   Program Counter
  //   CPU
  //   Din
  //   Dout
  //   @
  //   WR#RD
  //   data memory
  //   tty
  //   keyboard
endmodule
