// Logisim project alu.circ as structural Verilog: 3 circuits, main circuit ALU
module ALU (
  input  AInvert,
  input  BNegate,
  input  [1:0] Operation,
  input  [31:0] A,
  input  [31:0] B,
  output Zero,
  output [31:0] Result,
  output Overflow,
  output Carry_out
);

  wire and_2_out, not_3_out, overflow_1_overflow;
  wire [0:0] xor_1_out;
  wire [31:0] adder_1_out, and_1_out, multiplexer_1_out, multiplexer_2_out, not_1_out, not_2_out, or_1_out;

  assign not_1_out = ~A;  // NOT_Gate not_1, 32 bits wide
  assign not_2_out = ~B;  // NOT_Gate not_2, 32 bits wide
  Multiplexer #(.width(32), .enable("false")) multiplexer_1 (
    .in0(A), .in1(not_1_out), .out(multiplexer_1_out), .sel(AInvert));
  Multiplexer #(.width(32), .enable("false")) multiplexer_2 (
    .in0(B), .in1(not_2_out), .out(multiplexer_2_out), .sel(BNegate));
  assign and_1_out = multiplexer_1_out & multiplexer_2_out;  // AND_Gate and_1, 32 bits wide
  assign or_1_out = multiplexer_1_out | multiplexer_2_out;  // OR_Gate or_1, 32 bits wide
  Adder #(.width(32)) adder_1 (
    .a(multiplexer_1_out), .b(multiplexer_2_out), .out(adder_1_out), .cin(BNegate), .cout(Carry_out));
  Overflow overflow_1 (.A(A), .B(B), .Sign_of_result(adder_1_out[31]), .Sub(BNegate), .Overflow(overflow_1_overflow));
  xor xor_1 (xor_1_out[0], adder_1_out[31], overflow_1_overflow);
  Multiplexer #(.select(2), .width(32), .enable("false")) multiplexer_3 (
    .in0(and_1_out), .in1(or_1_out), .in2(adder_1_out), .in3({{31{1'b0}}, xor_1_out[0]}), .out(Result),
    .sel(Operation));
  not not_3 (not_3_out, Operation[0]);
  and and_2 (and_2_out, Operation[1], not_3_out);
  Zero zero_1 (.IsZero(Result), .Zero(Zero));
  and and_3 (Overflow, and_2_out, overflow_1_overflow);

  // Notes on the sheet:
  //   Sign bit
  //   Compute overflow
  //   We test the overflow only if operation is add or sub 
  //   IsZero?
endmodule

module Zero (
  input  [31:0] IsZero,
  output Zero
);

  wire or_1_out, or_2_out, or_3_out, or_4_out, or_5_out, or_6_out, or_7_out, or_8_out;

  or or_1 (or_1_out, IsZero[0], IsZero[1], IsZero[2], IsZero[3]);
  or or_2 (or_2_out, IsZero[4], IsZero[5], IsZero[6], IsZero[7]);
  or or_3 (or_3_out, IsZero[8], IsZero[9], IsZero[10], IsZero[11]);
  or or_4 (or_4_out, IsZero[12], IsZero[13], IsZero[14], IsZero[15]);
  or or_5 (or_5_out, IsZero[16], IsZero[17], IsZero[18], IsZero[19]);
  or or_6 (or_6_out, IsZero[20], IsZero[21], IsZero[22], IsZero[23]);
  or or_7 (or_7_out, IsZero[24], IsZero[25], IsZero[26], IsZero[27]);
  or or_8 (or_8_out, IsZero[28], IsZero[29], IsZero[30], IsZero[31]);
  nor nor_1 (Zero, or_1_out, or_2_out, or_3_out, or_4_out, or_5_out, or_6_out, or_7_out, or_8_out);
endmodule

module Overflow (
  input  Sign_of_result,
  input  Sub,
  input  [31:0] A,
  input  [31:0] B,
  output Overflow
);

  wire and_1_out, and_2_out, and_3_out, and_4_out, and_5_out, and_6_out, not_1_out, not_2_out, not_3_out,
       not_4_out, not_5_out, not_6_out, not_7_out, or_1_out, or_2_out;

  not not_1 (not_1_out, A[31]);
  and and_1 (and_1_out, Sign_of_result, not_1_out, not_2_out);
  not not_2 (not_2_out, B[31]);
  not not_3 (not_3_out, Sign_of_result);
  and and_2 (and_2_out, not_3_out, A[31], B[31]);
  and and_3 (and_3_out, Sign_of_result, not_4_out, B[31]);
  not not_4 (not_4_out, A[31]);
  not not_5 (not_5_out, Sign_of_result);
  and and_4 (and_4_out, not_5_out, A[31], not_6_out);
  not not_6 (not_6_out, B[31]);
  or or_1 (or_1_out, and_1_out, and_2_out);
  or or_2 (or_2_out, and_3_out, and_4_out);
  not not_7 (not_7_out, Sub);
  and and_5 (and_5_out, not_7_out, or_1_out);
  and and_6 (and_6_out, Sub, or_2_out);
  or or_3 (Overflow, and_5_out, and_6_out);
endmodule
