// Logisim project control.circ as structural Verilog: 1 circuit, main circuit Control
module Control (
  input  [5:0] Instruction__31_26,
  output RegDst,
  output Jump,
  output Branch,
  output MemRead,
  output MemToReg,
  output [1:0] ALUOp,
  output MemWrite,
  output ALUSrc,
  output RegWrite
);

  wire not_1_out, not_2_out, not_3_out, not_4_out, not_5_out, not_6_out, not_7_out, not_8_out, not_9_out,
       not_10_out, not_11_out, not_12_out, not_13_out, not_14_out, not_15_out, not_16_out, not_17_out,
       not_18_out, not_19_out, not_20_out, not_21_out;

  not not_1 (not_1_out, Instruction__31_26[0]);
  not not_2 (not_2_out, Instruction__31_26[1]);
  not not_3 (not_3_out, Instruction__31_26[2]);
  not not_4 (not_4_out, Instruction__31_26[4]);
  not not_5 (not_5_out, Instruction__31_26[5]);
  not not_6 (not_6_out, Instruction__31_26[3]);
  and and_1 (ALUOp[1], not_5_out, not_4_out, not_6_out, not_3_out, not_2_out, not_1_out);
  not not_7 (not_7_out, Instruction__31_26[3]);
  not not_8 (not_8_out, Instruction__31_26[2]);
  not not_9 (not_9_out, Instruction__31_26[4]);
  and and_2 (MemRead, Instruction__31_26[5], not_9_out, not_7_out, not_8_out, Instruction__31_26[1], Instruction__31_26[0]);
  not not_10 (not_10_out, Instruction__31_26[4]);
  not not_11 (not_11_out, Instruction__31_26[2]);
  and and_3 (MemWrite, Instruction__31_26[5], not_10_out, Instruction__31_26[3], not_11_out, Instruction__31_26[1], Instruction__31_26[0]);
  not not_12 (not_12_out, Instruction__31_26[5]);
  not not_13 (not_13_out, Instruction__31_26[4]);
  not not_14 (not_14_out, Instruction__31_26[3]);
  not not_15 (not_15_out, Instruction__31_26[1]);
  not not_16 (not_16_out, Instruction__31_26[0]);
  and and_4 (ALUOp[0], not_12_out, not_13_out, not_14_out, Instruction__31_26[2], not_15_out, not_16_out);
  not not_17 (not_17_out, Instruction__31_26[5]);
  not not_18 (not_18_out, Instruction__31_26[3]);
  not not_19 (not_19_out, Instruction__31_26[2]);
  not not_20 (not_20_out, Instruction__31_26[0]);
  not not_21 (not_21_out, Instruction__31_26[4]);
  and and_5 (Jump, not_17_out, not_21_out, not_18_out, not_19_out, Instruction__31_26[1], not_20_out);
  or or_1 (ALUSrc, MemRead, MemWrite);
  or or_2 (RegWrite, ALUOp[1], MemRead);

  assign Branch = ALUOp[0];
  assign MemToReg = MemRead;
  assign RegDst = ALUOp[1];

  // Notes on the sheet:
  //   R-format
  //   lw
  //   sw
  //   beq
  //   jump
endmodule
