// Logisim project mips32_mono.circ as structural Verilog: 1 circuit, main circuit MIPS32
module MIPS32 (
  input  Reset
);

  wire alu_1_zero, and_1_out, Clock_out, control_1_alusrc, control_1_branch, control_1_jump,
       control_1_memread, control_1_memtoreg, control_1_memwrite, control_1_regdst, control_1_regwrite;
  wire [1:0] control_1_aluop;
  wire [2:0] alu_control_1_operation;
  wire [4:0] multiplexer_1_out;
  wire [31:0] adder_1_out, adder_2_out, alu_1_result, multiplexer_2_out, multiplexer_3_out,
       multiplexer_4_out, multiplexer_5_out, ram_1_mem_data, register_1_q, registerfile32_1_read_data_1,
       registerfile32_1_read_data_2, rom_1_mem_data, shift_left_2_1_out, shift_left_2_2_out,
       sign_extend_1_out;

  Register #(.width(32)) register_1 (
    .D(multiplexer_3_out), .Q(register_1_q), .clk(Clock_out), .clr(Reset));  // open: en
  Adder #(.width(32)) adder_1 (.a(32'h4), .b(register_1_q), .out(adder_1_out), .cin(1'b0));  // open: cout
  rom rom_1 (.Address(register_1_q[21:0]), .Sel(1'b1), .Mem_data(rom_1_mem_data));
  Shift_left_2 shift_left_2_1 (.In({{6{1'b0}}, rom_1_mem_data[25:0]}), .Out(shift_left_2_1_out));
  Control control_1 (
    .Instruction__31_26(rom_1_mem_data[31:26]), .RegDst(control_1_regdst), .Jump(control_1_jump),
    .Branch(control_1_branch), .MemRead(control_1_memread), .MemToReg(control_1_memtoreg),
    .ALUOp(control_1_aluop), .MemWrite(control_1_memwrite), .ALUSrc(control_1_alusrc),
    .RegWrite(control_1_regwrite));
  Multiplexer #(.width(5), .enable("false")) multiplexer_1 (
    .in0(rom_1_mem_data[20:16]), .in1(rom_1_mem_data[15:11]), .out(multiplexer_1_out), .sel(control_1_regdst));
  Sign_extend sign_extend_1 (.In(rom_1_mem_data[15:0]), .Out(sign_extend_1_out));
  RegisterFile32 registerfile32_1 (
    .Read_register_number_1(rom_1_mem_data[25:21]), .Read_register_number_2(rom_1_mem_data[20:16]),
    .Write_register(multiplexer_1_out), .Write_data(multiplexer_5_out), .Write(control_1_regwrite),
    .Clock(Clock_out), .Read_data_1(registerfile32_1_read_data_1), .Read_data_2(registerfile32_1_read_data_2));
  Shift_left_2 shift_left_2_2 (.In(sign_extend_1_out), .Out(shift_left_2_2_out));
  Adder #(.width(32)) adder_2 (.a(adder_1_out), .b(shift_left_2_2_out), .out(adder_2_out), .cin(1'b0));  // open: cout
  Multiplexer #(.width(32), .enable("false")) multiplexer_2 (
    .in0(adder_1_out), .in1(adder_2_out), .out(multiplexer_2_out), .sel(and_1_out));
  Clock Clock (.out(Clock_out));
  Multiplexer #(.width(32), .enable("false")) multiplexer_3 (
    .in0(multiplexer_2_out), .in1({adder_1_out[31:28], shift_left_2_1_out[27:0]}), .out(multiplexer_3_out),
    .sel(control_1_jump));
  ALU_control alu_control_1 (.F(rom_1_mem_data[5:0]), .ALUOp(control_1_aluop), .Operation(alu_control_1_operation));
  Multiplexer #(.width(32), .enable("false")) multiplexer_4 (
    .in0(registerfile32_1_read_data_2), .in1(sign_extend_1_out), .out(multiplexer_4_out),
    .sel(control_1_alusrc));
  and and_1 (and_1_out, control_1_branch, alu_1_zero);
  ALU alu_1 (
    .A(registerfile32_1_read_data_1), .B(multiplexer_4_out), .Zero(alu_1_zero), .Result(alu_1_result),
    .AInvert(1'b0), .BNegate(alu_control_1_operation[2]), .Operation(alu_control_1_operation[1:0]));  // open: Overflow, Carry_out
  ram ram_1 (
    .Address(alu_1_result[21:0]), .Write_data(registerfile32_1_read_data_2), .Mem_read(control_1_memread),
    .Mem_write(control_1_memwrite), .Sel(1'b1), .Clock(Clock_out), .Mem_data(ram_1_mem_data));
  Multiplexer #(.width(32), .enable("false")) multiplexer_5 (
    .in0(alu_1_result), .in1(ram_1_mem_data), .out(multiplexer_5_out), .sel(control_1_memtoreg));

  // Notes on the sheet:
  //   PC
  //   PC + 4 
  //   Instruction memory
  //   (4Mo)
  //   Shift left 2
  //   [25-0]
  //   [15-0]
  //   [27-0]
  //   Control
  //   [31-26]
  //   [25-21]
  //   [20-16]
  //   [15-11]
  //   [5-0]
  //   PC + 4 [31-28]
  //   RegDst
  //   RegWrite
  //   Read rg1
  //   Read rg2
  //   Write rg
  //   Sign extend
  //   Jump address [31-0]
  //   Register file
  //   Write data
  //   [31-0]
  //   Shift left 2
  //   Read data1
  //   Read data2
  //   Jump
  //   ALUOp
  //   ALU control
  //   ALUSrc
  //   Branch
  //   ALU
  //   Zero
  //   MemRead
  //   Address
  //   Write data
  //   MemWrite
  //   Data memory
  //   (4Mo)
  //   MemToReg
endmodule
