// Logisim project register_file.circ as structural Verilog: 9 circuits, main circuit RegisterFile4
module RegisterFile4 (
  input  [1:0] Read_register_number_1,
  input  [1:0] Read_register_number_2,
  input  [1:0] Write_register,
  input  [31:0] Write_data,
  input  Write,
  input  Clock,
  output [31:0] Read_data_1,
  output [31:0] Read_data_2
);

  wire demultiplexer_1_out0, demultiplexer_1_out1, demultiplexer_1_out2, demultiplexer_1_out3;
  wire [31:0] register32_1_dout, register32_2_dout, register32_3_dout, register32_4_dout;

  Demultiplexer #(.select(2), .enable("false")) demultiplexer_1 (
    .out0(demultiplexer_1_out0), .out1(demultiplexer_1_out1), .out2(demultiplexer_1_out2),
    .out3(demultiplexer_1_out3), .in(Write), .sel(Write_register));
  Register32 register32_1 (
    .Din(Write_data), .Load(demultiplexer_1_out0), .Clock(Clock), .Clear(1'b0), .Dout(register32_1_dout));
  Register32 register32_2 (
    .Din(Write_data), .Load(demultiplexer_1_out1), .Clock(Clock), .Clear(1'b0), .Dout(register32_2_dout));
  Register32 register32_3 (
    .Din(Write_data), .Load(demultiplexer_1_out2), .Clock(Clock), .Clear(1'b0), .Dout(register32_3_dout));
  Register32 register32_4 (
    .Din(Write_data), .Load(demultiplexer_1_out3), .Clock(Clock), .Clear(1'b0), .Dout(register32_4_dout));
  Multiplexer #(.select(2), .width(32), .enable("false")) multiplexer_1 (
    .in0(register32_1_dout), .in1(register32_2_dout), .in2(register32_3_dout), .in3(register32_4_dout),
    .out(Read_data_1), .sel(Read_register_number_1));
  Multiplexer #(.select(2), .width(32), .enable("false")) multiplexer_2 (
    .in0(register32_1_dout), .in1(register32_2_dout), .in2(register32_3_dout), .in3(register32_4_dout),
    .out(Read_data_2), .sel(Read_register_number_2));
endmodule

module Register32 (
  input  Load,
  input  [31:0] Din,
  input  Clock,
  input  Clear,
  output [31:0] Dout
);

  wire [31:0] multiplexer_1_out;

  Multiplexer #(.width(32), .enable("false")) multiplexer_1 (
    .in0(Dout), .in1(Din), .out(multiplexer_1_out), .sel(Load));
  Register #(.width(32)) register_1 (.D(multiplexer_1_out), .Q(Dout), .clk(Clock), .clr(Clear));  // open: en
endmodule

module RegisterFile32 (
  input  [4:0] Read_register_number_1,
  input  [4:0] Read_register_number_2,
  input  [4:0] Write_register,
  input  [31:0] Write_data,
  input  Write,
  input  Clock,
  output [31:0] Read_data_1,
  output [31:0] Read_data_2
);

  wire demultiplexer_1_out0, demultiplexer_1_out1, demultiplexer_1_out2, demultiplexer_1_out3,
       demultiplexer_1_out4, demultiplexer_1_out5, demultiplexer_1_out6, demultiplexer_1_out7;
  wire [31:0] registerfile4_1_read_data_1, registerfile4_1_read_data_2, registerfile4_2_read_data_1,
       registerfile4_2_read_data_2, registerfile4_3_read_data_1, registerfile4_3_read_data_2,
       registerfile4_4_read_data_1, registerfile4_4_read_data_2, registerfile4_5_read_data_1,
       registerfile4_5_read_data_2, registerfile4_6_read_data_1, registerfile4_6_read_data_2,
       registerfile4_7_read_data_1, registerfile4_7_read_data_2, registerfile4with0_1_read_data_1,
       registerfile4with0_1_read_data_2;

  Demultiplexer #(.select(3), .enable("false")) demultiplexer_1 (
    .out0(demultiplexer_1_out0), .out1(demultiplexer_1_out1), .out2(demultiplexer_1_out2),
    .out3(demultiplexer_1_out3), .out4(demultiplexer_1_out4), .out5(demultiplexer_1_out5),
    .out6(demultiplexer_1_out6), .out7(demultiplexer_1_out7), .in(Write), .sel(Write_register[4:2]));
  RegisterFile4With0 registerfile4with0_1 (
    .Read_register_number_1(Read_register_number_1[1:0]),
    .Read_register_number_2(Read_register_number_2[1:0]), .Write_register(Write_register[1:0]),
    .Write_data(Write_data), .Write(demultiplexer_1_out0), .Clock(Clock),
    .Read_data_1(registerfile4with0_1_read_data_1), .Read_data_2(registerfile4with0_1_read_data_2));
  RegisterFile4 registerfile4_1 (
    .Read_register_number_1(Read_register_number_1[1:0]),
    .Read_register_number_2(Read_register_number_2[1:0]), .Write_register(Write_register[1:0]),
    .Write_data(Write_data), .Write(demultiplexer_1_out1), .Clock(Clock),
    .Read_data_1(registerfile4_1_read_data_1), .Read_data_2(registerfile4_1_read_data_2));
  RegisterFile4 registerfile4_2 (
    .Read_register_number_1(Read_register_number_1[1:0]),
    .Read_register_number_2(Read_register_number_2[1:0]), .Write_register(Write_register[1:0]),
    .Write_data(Write_data), .Write(demultiplexer_1_out2), .Clock(Clock),
    .Read_data_1(registerfile4_2_read_data_1), .Read_data_2(registerfile4_2_read_data_2));
  RegisterFile4 registerfile4_3 (
    .Read_register_number_1(Read_register_number_1[1:0]),
    .Read_register_number_2(Read_register_number_2[1:0]), .Write_register(Write_register[1:0]),
    .Write_data(Write_data), .Write(demultiplexer_1_out3), .Clock(Clock),
    .Read_data_1(registerfile4_3_read_data_1), .Read_data_2(registerfile4_3_read_data_2));
  RegisterFile4 registerfile4_4 (
    .Read_register_number_1(Read_register_number_1[1:0]),
    .Read_register_number_2(Read_register_number_2[1:0]), .Write_register(Write_register[1:0]),
    .Write_data(Write_data), .Write(demultiplexer_1_out4), .Clock(Clock),
    .Read_data_1(registerfile4_4_read_data_1), .Read_data_2(registerfile4_4_read_data_2));
  RegisterFile4 registerfile4_5 (
    .Read_register_number_1(Read_register_number_1[1:0]),
    .Read_register_number_2(Read_register_number_2[1:0]), .Write_register(Write_register[1:0]),
    .Write_data(Write_data), .Write(demultiplexer_1_out5), .Clock(Clock),
    .Read_data_1(registerfile4_5_read_data_1), .Read_data_2(registerfile4_5_read_data_2));
  RegisterFile4 registerfile4_6 (
    .Read_register_number_1(Read_register_number_1[1:0]),
    .Read_register_number_2(Read_register_number_2[1:0]), .Write_register(Write_register[1:0]),
    .Write_data(Write_data), .Write(demultiplexer_1_out6), .Clock(Clock),
    .Read_data_1(registerfile4_6_read_data_1), .Read_data_2(registerfile4_6_read_data_2));
  RegisterFile4 registerfile4_7 (
    .Read_register_number_1(Read_register_number_1[1:0]),
    .Read_register_number_2(Read_register_number_2[1:0]), .Write_register(Write_register[1:0]),
    .Write_data(Write_data), .Write(demultiplexer_1_out7), .Clock(Clock),
    .Read_data_1(registerfile4_7_read_data_1), .Read_data_2(registerfile4_7_read_data_2));
  Multiplexer #(.select(3), .width(32), .enable("false")) multiplexer_1 (
    .in0(registerfile4with0_1_read_data_1), .in1(registerfile4_1_read_data_1),
    .in2(registerfile4_2_read_data_1), .in3(registerfile4_3_read_data_1), .in4(registerfile4_4_read_data_1),
    .in5(registerfile4_5_read_data_1), .in6(registerfile4_6_read_data_1), .in7(registerfile4_7_read_data_1),
    .out(Read_data_1), .sel(Read_register_number_1[4:2]));
  Multiplexer #(.select(3), .width(32), .enable("false")) multiplexer_2 (
    .in0(registerfile4with0_1_read_data_2), .in1(registerfile4_1_read_data_2),
    .in2(registerfile4_2_read_data_2), .in3(registerfile4_3_read_data_2), .in4(registerfile4_4_read_data_2),
    .in5(registerfile4_5_read_data_2), .in6(registerfile4_6_read_data_2), .in7(registerfile4_7_read_data_2),
    .out(Read_data_2), .sel(Read_register_number_2[4:2]));
endmodule

module RegisterFile4With0 (
  input  [1:0] Read_register_number_1,
  input  [1:0] Read_register_number_2,
  input  [1:0] Write_register,
  input  [31:0] Write_data,
  input  Write,
  input  Clock,
  output [31:0] Read_data_1,
  output [31:0] Read_data_2
);

  wire demultiplexer_1_out0, demultiplexer_1_out1, demultiplexer_1_out2, demultiplexer_1_out3;
  wire [31:0] register32_1_dout, register32_2_dout, register32_3_dout;

  Demultiplexer #(.select(2), .enable("false")) demultiplexer_1 (
    .out0(demultiplexer_1_out0), .out1(demultiplexer_1_out1), .out2(demultiplexer_1_out2),
    .out3(demultiplexer_1_out3), .in(Write), .sel(Write_register));
  Register32 register32_1 (
    .Din(Write_data), .Load(demultiplexer_1_out1), .Clock(Clock), .Clear(1'b0), .Dout(register32_1_dout));
  Register32 register32_2 (
    .Din(Write_data), .Load(demultiplexer_1_out2), .Clock(Clock), .Clear(1'b0), .Dout(register32_2_dout));
  Register32 register32_3 (
    .Din(Write_data), .Load(demultiplexer_1_out3), .Clock(Clock), .Clear(1'b0), .Dout(register32_3_dout));
  Multiplexer #(.select(2), .width(32), .enable("false")) multiplexer_1 (
    .in0({32{1'b0}}), .in1(register32_1_dout), .in2(register32_2_dout), .in3(register32_3_dout),
    .out(Read_data_1), .sel(Read_register_number_1));
  Multiplexer #(.select(2), .width(32), .enable("false")) multiplexer_2 (
    .in0({32{1'b0}}), .in1(register32_1_dout), .in2(register32_2_dout), .in3(register32_3_dout),
    .out(Read_data_2), .sel(Read_register_number_2));
endmodule

module Coprocessor0_8WithStatus (
  input  Set_EXL,
  input  Reset_EXL,
  input  [2:0] Read_register_number,
  input  [2:0] Write_register_number,
  input  [31:0] Write_data,
  input  Write,
  input  Clock,
  input  Init,
  output [31:0] Read_data,
  output [31:0] Status
);

  wire demultiplexer_1_out0, demultiplexer_1_out1, demultiplexer_1_out2, demultiplexer_1_out3,
       demultiplexer_1_out4, demultiplexer_1_out5, demultiplexer_1_out6, demultiplexer_1_out7;
  wire [31:0] register32_1_dout, register32_2_dout, register32_3_dout, register32_4_dout, register32_5_dout,
       register32_6_dout, register32_7_dout;

  Demultiplexer #(.select(3), .enable("false")) demultiplexer_1 (
    .out0(demultiplexer_1_out0), .out1(demultiplexer_1_out1), .out2(demultiplexer_1_out2),
    .out3(demultiplexer_1_out3), .out4(demultiplexer_1_out4), .out5(demultiplexer_1_out5),
    .out6(demultiplexer_1_out6), .out7(demultiplexer_1_out7), .in(Write), .sel(Write_register_number));
  Register32 register32_1 (
    .Din(Write_data), .Load(demultiplexer_1_out0), .Clock(Clock), .Clear(Init), .Dout(register32_1_dout));
  Register32 register32_2 (
    .Load(demultiplexer_1_out1), .Clock(Clock), .Clear(Init), .Dout(register32_2_dout));  // open: Din
  Register32 register32_3 (
    .Din(Write_data), .Load(demultiplexer_1_out2), .Clock(Clock), .Clear(Init), .Dout(register32_3_dout));
  Register32 register32_4 (
    .Din(Write_data), .Load(demultiplexer_1_out3), .Clock(Clock), .Clear(Init), .Dout(register32_4_dout));
  Satus_register satus_register_1 (
    .Din(Write_data), .Load(demultiplexer_1_out4), .Set_EXL(Set_EXL), .Reset_EXL(Reset_EXL), .Clock(Clock),
    .Init(Init), .Dout(Status));
  Register32 register32_5 (
    .Din(Write_data), .Load(demultiplexer_1_out5), .Clock(Clock), .Clear(Init), .Dout(register32_5_dout));
  Register32 register32_6 (
    .Din(Write_data), .Load(demultiplexer_1_out6), .Clock(Clock), .Clear(Init), .Dout(register32_6_dout));
  Register32 register32_7 (
    .Din(Write_data), .Load(demultiplexer_1_out7), .Clock(Clock), .Clear(Init), .Dout(register32_7_dout));
  Multiplexer #(.select(3), .width(32), .enable("false")) multiplexer_1 (
    .in0(register32_1_dout), .in1(register32_2_dout), .in2(register32_3_dout), .in3(register32_4_dout),
    .in4(Status), .in5(register32_5_dout), .in6(register32_6_dout), .in7(register32_7_dout), .out(Read_data),
    .sel(Read_register_number));
endmodule

module Satus_register (
  input  Load,
  input  Set_EXL,
  input  Reset_EXL,
  input  [31:0] Din,
  input  Clock,
  input  Init,
  output [31:0] Dout
);

  wire or_1_out;
  wire [31:0] multiplexer_1_out, multiplexer_2_out;

  Multiplexer #(.width(32), .enable("false")) multiplexer_1 (
    .in0(Dout), .in1(Din), .out(multiplexer_1_out), .sel(Load));
  Multiplexer #(.width(32), .enable("false")) multiplexer_2 (
    .in0(multiplexer_1_out), .in1({multiplexer_1_out[31:2], Set_EXL, multiplexer_1_out[0]}),
    .out(multiplexer_2_out), .sel(or_1_out));
  or or_1 (or_1_out, Set_EXL, Reset_EXL);
  Register #(.width(32)) register_1 (.D(multiplexer_2_out), .Q(Dout), .clk(Clock), .clr(Init));  // open: en
endmodule

module Coprocessor0_8 (
  input  [2:0] Read_register_number,
  input  [2:0] Write_register_number,
  input  [31:0] Write_data,
  input  Write,
  input  Clock,
  input  Init,
  output [31:0] Read_data
);

  wire demultiplexer_1_out0, demultiplexer_1_out1, demultiplexer_1_out2, demultiplexer_1_out3,
       demultiplexer_1_out4, demultiplexer_1_out5, demultiplexer_1_out6, demultiplexer_1_out7;
  wire [31:0] register32_1_dout, register32_2_dout, register32_3_dout, register32_4_dout, register32_5_dout,
       register32_6_dout, register32_7_dout, register32_8_dout;

  Demultiplexer #(.select(3), .enable("false")) demultiplexer_1 (
    .out0(demultiplexer_1_out0), .out1(demultiplexer_1_out1), .out2(demultiplexer_1_out2),
    .out3(demultiplexer_1_out3), .out4(demultiplexer_1_out4), .out5(demultiplexer_1_out5),
    .out6(demultiplexer_1_out6), .out7(demultiplexer_1_out7), .in(Write), .sel(Write_register_number));
  Register32 register32_1 (
    .Din(Write_data), .Load(demultiplexer_1_out0), .Clock(Clock), .Clear(Init), .Dout(register32_1_dout));
  Register32 register32_2 (
    .Din(Write_data), .Load(demultiplexer_1_out1), .Clock(Clock), .Clear(Init), .Dout(register32_2_dout));
  Register32 register32_3 (
    .Din(Write_data), .Load(demultiplexer_1_out2), .Clock(Clock), .Clear(Init), .Dout(register32_3_dout));
  Register32 register32_4 (
    .Din(Write_data), .Load(demultiplexer_1_out3), .Clock(Clock), .Clear(Init), .Dout(register32_4_dout));
  Register32 register32_5 (
    .Din(Write_data), .Load(demultiplexer_1_out4), .Clock(Clock), .Clear(Init), .Dout(register32_5_dout));
  Register32 register32_6 (
    .Din(Write_data), .Load(demultiplexer_1_out5), .Clock(Clock), .Clear(Init), .Dout(register32_6_dout));
  Register32 register32_7 (
    .Din(Write_data), .Load(demultiplexer_1_out6), .Clock(Clock), .Clear(Init), .Dout(register32_7_dout));
  Register32 register32_8 (
    .Din(Write_data), .Load(demultiplexer_1_out7), .Clock(Clock), .Clear(Init), .Dout(register32_8_dout));
  Multiplexer #(.select(3), .width(32), .enable("false")) multiplexer_1 (
    .in0(register32_1_dout), .in1(register32_2_dout), .in2(register32_3_dout), .in3(register32_4_dout),
    .in4(register32_5_dout), .in5(register32_6_dout), .in6(register32_7_dout), .in7(register32_8_dout),
    .out(Read_data), .sel(Read_register_number));
endmodule

module Coprocessor0RegisterFile (
  input  Set_EXL,
  input  Reset_EXL,
  input  [4:0] Read_register_number,
  input  [4:0] Write_register_number,
  input  [31:0] Write_data,
  input  Write,
  input  Clock,
  input  Init,
  output [31:0] Read_data,
  output [31:0] Status,
  output [31:0] Base,
  output [31:0] Limit
);

  wire demultiplexer_1_out0, demultiplexer_1_out1, demultiplexer_1_out2, demultiplexer_1_out3;
  wire [31:0] coprocessor0_8_1_read_data, coprocessor0_8_2_read_data,
       coprocessor0_8withbaseandlimit_1_read_data, coprocessor0_8withstatus_1_read_data;

  Demultiplexer #(.select(2), .enable("false")) demultiplexer_1 (
    .out0(demultiplexer_1_out0), .out1(demultiplexer_1_out1), .out2(demultiplexer_1_out2),
    .out3(demultiplexer_1_out3), .in(Write), .sel(Write_register_number[4:3]));
  Coprocessor0_8WithBaseAndLimit coprocessor0_8withbaseandlimit_1 (
    .Read_register_number(Read_register_number[2:0]), .Write_register_number(Write_register_number[2:0]),
    .Write_data(Write_data), .Write(demultiplexer_1_out0), .Clock(Clock), .Init(Init),
    .Read_data(coprocessor0_8withbaseandlimit_1_read_data), .Base(Base), .Limit(Limit));
  Coprocessor0_8WithStatus coprocessor0_8withstatus_1 (
    .Read_register_number(Read_register_number[2:0]), .Write_register_number(Write_register_number[2:0]),
    .Write_data(Write_data), .Set_EXL(Set_EXL), .Reset_EXL(Reset_EXL), .Write(demultiplexer_1_out1),
    .Clock(Clock), .Init(Init), .Read_data(coprocessor0_8withstatus_1_read_data), .Status(Status));
  Coprocessor0_8 coprocessor0_8_1 (
    .Read_register_number(Read_register_number[2:0]), .Write_register_number(Write_register_number[2:0]),
    .Write_data(Write_data), .Write(demultiplexer_1_out2), .Clock(Clock), .Init(Init),
    .Read_data(coprocessor0_8_1_read_data));
  Coprocessor0_8 coprocessor0_8_2 (
    .Read_register_number(Read_register_number[2:0]), .Write_register_number(Write_register_number[2:0]),
    .Write_data(Write_data), .Write(demultiplexer_1_out3), .Clock(Clock), .Init(Init),
    .Read_data(coprocessor0_8_2_read_data));
  Multiplexer #(.select(2), .width(32), .enable("false")) multiplexer_1 (
    .in0(coprocessor0_8withbaseandlimit_1_read_data), .in1(coprocessor0_8withstatus_1_read_data),
    .in2(coprocessor0_8_1_read_data), .in3(coprocessor0_8_2_read_data), .out(Read_data),
    .sel(Read_register_number[4:3]));
endmodule

module Coprocessor0_8WithBaseAndLimit (
  input  [2:0] Read_register_number,
  input  [2:0] Write_register_number,
  input  [31:0] Write_data,
  input  Write,
  input  Clock,
  input  Init,
  output [31:0] Read_data,
  output [31:0] Base,
  output [31:0] Limit
);

  wire demultiplexer_1_out0, demultiplexer_1_out1, demultiplexer_1_out2, demultiplexer_1_out3,
       demultiplexer_1_out4, demultiplexer_1_out5, demultiplexer_1_out6, demultiplexer_1_out7;
  wire [31:0] register32_3_dout, register32_4_dout, register32_5_dout, register32_6_dout, register32_7_dout,
       register32_8_dout;

  Demultiplexer #(.select(3), .enable("false")) demultiplexer_1 (
    .out0(demultiplexer_1_out0), .out1(demultiplexer_1_out1), .out2(demultiplexer_1_out2),
    .out3(demultiplexer_1_out3), .out4(demultiplexer_1_out4), .out5(demultiplexer_1_out5),
    .out6(demultiplexer_1_out6), .out7(demultiplexer_1_out7), .in(Write), .sel(Write_register_number));
  Register32 register32_1 (.Din(Write_data), .Load(demultiplexer_1_out0), .Clock(Clock), .Clear(Init), .Dout(Base));
  Register32 register32_2 (.Din(Write_data), .Load(demultiplexer_1_out1), .Clock(Clock), .Clear(Init), .Dout(Limit));
  Register32 register32_3 (
    .Din(Write_data), .Load(demultiplexer_1_out2), .Clock(Clock), .Clear(Init), .Dout(register32_3_dout));
  Register32 register32_4 (
    .Din(Write_data), .Load(demultiplexer_1_out3), .Clock(Clock), .Clear(Init), .Dout(register32_4_dout));
  Register32 register32_5 (
    .Din(Write_data), .Load(demultiplexer_1_out4), .Clock(Clock), .Clear(Init), .Dout(register32_5_dout));
  Register32 register32_6 (
    .Din(Write_data), .Load(demultiplexer_1_out5), .Clock(Clock), .Clear(Init), .Dout(register32_6_dout));
  Register32 register32_7 (
    .Din(Write_data), .Load(demultiplexer_1_out6), .Clock(Clock), .Clear(Init), .Dout(register32_7_dout));
  Register32 register32_8 (
    .Din(Write_data), .Load(demultiplexer_1_out7), .Clock(Clock), .Clear(Init), .Dout(register32_8_dout));
  Multiplexer #(.select(3), .width(32), .enable("false")) multiplexer_1 (
    .in0(Base), .in1(Limit), .in2(register32_3_dout), .in3(register32_4_dout), .in4(register32_5_dout),
    .in5(register32_6_dout), .in6(register32_7_dout), .in7(register32_8_dout), .out(Read_data),
    .sel(Read_register_number));
endmodule
