// Logisim project shift_left2.circ as structural Verilog: 2 circuits, main circuit Shift left 2
module Shift_left_2 (
  input  [31:0] In,
  output [31:0] Out
);


  assign Out = {In[29:0], 2'b00};
endmodule

module Sign_extend (
  input  [15:0] In,
  output [31:0] Out
);


  assign Out = {{17{In[15]}}, In[14:0]};
endmodule
