// Logisim project alu_control.circ as structural Verilog: 1 circuit, main circuit ALU control
module ALU_control (
  input  [1:0] ALUOp,
  input  [5:0] F,
  output [2:0] Operation
);

  wire and_1_out, or_1_out;

  or or_1 (or_1_out, F[3], F[0]);
  and and_1 (and_1_out, ALUOp[1], F[1]);
  and and_2 (Operation[0], ALUOp[1], or_1_out);
  or or_2 (Operation[2], ALUOp[0], and_1_out);
  nand nand_1 (Operation[1], ALUOp[1], F[2]);
endmodule
