// Logisim project memory.circ as structural Verilog: 3 circuits, main circuit ram16Ko
module ram16Ko (
  input  [13:0] A,
  input  [1:0] mode,
  input  [31:0] Din,
  input  sel,
  input  clock,
  input  out,
  output [31:0] Dout
);

  wire and_1_out, and_2_out, and_3_out, and_4_out, and_5_out, and_6_out, and_7_out, and_8_out, and_9_out,
       and_10_out, and_11_out, and_12_out, and_13_out, decoder_1_out0, decoder_1_out1, decoder_1_out2,
       decoder_1_out3, demultiplexer_1_out0, demultiplexer_1_out1, demultiplexer_1_out2,
       demultiplexer_1_out3, demultiplexer_2_out0, demultiplexer_2_out1, demultiplexer_2_out2,
       demultiplexer_2_out3, not_1_out, or_1_out, or_2_out, or_3_out, or_4_out, or_5_out, or_6_out;
  wire [7:0] controlled_buffer_12_out, controlled_buffer_12_out_2, controlled_buffer_13_out,
       controlled_buffer_13_out_2, ram_1_data, ram_2_data, ram_3_data, ram_4_data;

  Demultiplexer #(.select(2), .enable("false")) demultiplexer_1 (
    .out0(demultiplexer_1_out0), .out1(demultiplexer_1_out1), .out2(demultiplexer_1_out2),
    .out3(demultiplexer_1_out3), .in(sel), .sel(mode));
  Demultiplexer #(.select(2), .enable("false")) demultiplexer_2 (
    .out0(demultiplexer_2_out0), .out1(demultiplexer_2_out1), .out2(demultiplexer_2_out2),
    .out3(demultiplexer_2_out3), .in(sel), .sel(A[1:0]));
  or or_1 (or_1_out, demultiplexer_1_out0, demultiplexer_1_out1);
  and and_1 (and_1_out, demultiplexer_2_out0, demultiplexer_1_out2);
  and and_2 (and_2_out, demultiplexer_2_out0, or_1_out);
  and and_3 (and_3_out, demultiplexer_2_out1, or_1_out);
  and and_4 (and_4_out, demultiplexer_2_out0, demultiplexer_1_out3);
  and and_5 (and_5_out, demultiplexer_2_out3, or_1_out);
  and and_6 (and_6_out, demultiplexer_2_out2, or_1_out);
  and and_7 (and_7_out, demultiplexer_2_out2, demultiplexer_1_out2);
  or or_2 (or_2_out, and_2_out, and_1_out, and_4_out);
  or or_3 (or_3_out, and_3_out, and_1_out, and_4_out);
  or or_4 (or_4_out, and_6_out, and_7_out, and_4_out);
  or or_5 (or_5_out, and_5_out, and_7_out, and_4_out);
  not not_1 (not_1_out, out);
  Decoder #(.select(2), .enable("false")) decoder_1 (
    .out0(decoder_1_out0), .out1(decoder_1_out1), .out2(decoder_1_out2), .out3(decoder_1_out3), .sel(mode));
  or or_6 (or_6_out, decoder_1_out0, decoder_1_out1);
  RAM #(.addrWidth(12)) ram_1 (.addr(A[13:2]), .data(ram_1_data), .sel(or_2_out), .clk(clock), .ld(out));  // open: clr
  RAM #(.addrWidth(12)) ram_2 (.addr(A[13:2]), .data(ram_2_data), .sel(or_3_out), .clk(clock), .ld(out));  // open: clr
  RAM #(.addrWidth(12)) ram_3 (.addr(A[13:2]), .data(ram_3_data), .sel(or_4_out), .clk(clock), .ld(out));  // open: clr
  RAM #(.addrWidth(12)) ram_4 (.addr(A[13:2]), .data(ram_4_data), .sel(or_5_out), .clk(clock), .ld(out));  // open: clr
  and and_8 (and_8_out, or_6_out, out);
  and and_9 (and_9_out, or_6_out, not_1_out);
  and and_10 (and_10_out, decoder_1_out2, out);
  and and_11 (and_11_out, decoder_1_out2, not_1_out);
  and and_12 (and_12_out, decoder_1_out3, out);
  and and_13 (and_13_out, decoder_1_out3, not_1_out);
  assign Dout[7:0] = and_8_out ? ram_1_data : 8'bz;  // Controlled_Buffer controlled_buffer_1
  assign Dout[7:0] = and_8_out ? ram_2_data : 8'bz;  // Controlled_Buffer controlled_buffer_2
  assign Dout[7:0] = and_8_out ? ram_3_data : 8'bz;  // Controlled_Buffer controlled_buffer_3
  assign Dout[7:0] = and_8_out ? ram_4_data : 8'bz;  // Controlled_Buffer controlled_buffer_4
  assign ram_1_data = and_9_out ? Din[7:0] : 8'bz;  // Controlled_Buffer controlled_buffer_5
  assign ram_2_data = and_9_out ? Din[7:0] : 8'bz;  // Controlled_Buffer controlled_buffer_6
  assign ram_3_data = and_9_out ? Din[7:0] : 8'bz;  // Controlled_Buffer controlled_buffer_7
  assign ram_4_data = and_9_out ? Din[7:0] : 8'bz;  // Controlled_Buffer controlled_buffer_8
  assign Dout = and_12_out ? {ram_1_data, ram_2_data, ram_3_data, ram_4_data} : 32'bz;  // Controlled_Buffer controlled_buffer_9
  assign {ram_1_data, ram_2_data, ram_3_data, ram_4_data} = and_13_out ? Din : 32'bz;  // Controlled_Buffer controlled_buffer_10
  assign Dout = and_10_out ? {controlled_buffer_12_out_2, controlled_buffer_12_out, ram_1_data, ram_2_data} : 32'bz;  // Controlled_Buffer controlled_buffer_11
  assign {controlled_buffer_12_out_2, controlled_buffer_12_out, ram_1_data, ram_2_data} = and_11_out ? Din : 32'bz;  // Controlled_Buffer controlled_buffer_12
  assign {controlled_buffer_13_out_2, controlled_buffer_13_out, ram_3_data, ram_4_data} = and_11_out ? Din : 32'bz;  // Controlled_Buffer controlled_buffer_13
  assign Dout = and_10_out ? {controlled_buffer_13_out_2, controlled_buffer_13_out, ram_3_data, ram_4_data} : 32'bz;  // Controlled_Buffer controlled_buffer_14

  // Notes on the sheet:
  //   A13..A2
  //   A1A0
  //   m8
  //   m16
  //   m32
  //   (m8./A1./A0 + m16./A1./A0 + m32./A1./A0).sel
  //   (m8./A1.A0 + m16./A1./A0 + m32./A1./A0).sel
  //   (m8.A1./A0 + m16.A1./A0 + m32./A1./A0).sel
  //   (m8.A1.A0 + m16.A1./A0 + m32./A1./A0).sel
  //   m8
  //   m16
  //   @ modulo 4 = 0
  //   @ modulo 4 = 1
  //   @ modulo 4 = 2
  //   @ modulo 4 = 3
  //   m32
  //   m8.out
  //   m8./out
  //   m16.out
  //   m16./out
  //   m32.out
  //   m32./out
endmodule

module ram256Ko (
  input  [17:0] A,
  input  [1:0] mode,
  input  [31:0] Din,
  input  sel,
  input  clock,
  input  out,
  output [31:0] Dout
);

  wire demultiplexer_1_out0, demultiplexer_1_out1, demultiplexer_1_out2, demultiplexer_1_out3,
       demultiplexer_1_out4, demultiplexer_1_out5, demultiplexer_1_out6, demultiplexer_1_out7,
       demultiplexer_1_out8, demultiplexer_1_out9, demultiplexer_1_out10, demultiplexer_1_out11,
       demultiplexer_1_out12, demultiplexer_1_out13, demultiplexer_1_out14, demultiplexer_1_out15;

  Demultiplexer #(.select(4), .enable("false")) demultiplexer_1 (
    .out0(demultiplexer_1_out0), .out1(demultiplexer_1_out1), .out2(demultiplexer_1_out2),
    .out3(demultiplexer_1_out3), .out4(demultiplexer_1_out4), .out5(demultiplexer_1_out5),
    .out6(demultiplexer_1_out6), .out7(demultiplexer_1_out7), .out8(demultiplexer_1_out8),
    .out9(demultiplexer_1_out9), .out10(demultiplexer_1_out10), .out11(demultiplexer_1_out11),
    .out12(demultiplexer_1_out12), .out13(demultiplexer_1_out13), .out14(demultiplexer_1_out14),
    .out15(demultiplexer_1_out15), .in(sel), .sel(A[17:14]));
  ram16Ko ram16ko_1 (
    .A(A[13:0]), .mode(mode), .sel(demultiplexer_1_out0), .clock(clock), .out(out), .Dout(Dout), .Din(Din));
  ram16Ko ram16ko_2 (
    .A(A[13:0]), .mode(mode), .sel(demultiplexer_1_out4), .clock(clock), .out(out), .Dout(Dout), .Din(Din));
  ram16Ko ram16ko_3 (
    .A(A[13:0]), .mode(mode), .sel(demultiplexer_1_out8), .clock(clock), .out(out), .Dout(Dout), .Din(Din));
  ram16Ko ram16ko_4 (
    .A(A[13:0]), .mode(mode), .sel(demultiplexer_1_out12), .clock(clock), .out(out), .Dout(Dout), .Din(Din));
  ram16Ko ram16ko_5 (
    .A(A[13:0]), .mode(mode), .sel(demultiplexer_1_out1), .clock(clock), .out(out), .Dout(Dout), .Din(Din));
  ram16Ko ram16ko_6 (
    .A(A[13:0]), .mode(mode), .sel(demultiplexer_1_out5), .clock(clock), .out(out), .Dout(Dout), .Din(Din));
  ram16Ko ram16ko_7 (
    .A(A[13:0]), .mode(mode), .sel(demultiplexer_1_out9), .clock(clock), .out(out), .Dout(Dout), .Din(Din));
  ram16Ko ram16ko_8 (
    .A(A[13:0]), .mode(mode), .sel(demultiplexer_1_out13), .clock(clock), .out(out), .Dout(Dout), .Din(Din));
  ram16Ko ram16ko_9 (
    .A(A[13:0]), .mode(mode), .sel(demultiplexer_1_out2), .clock(clock), .out(out), .Dout(Dout), .Din(Din));
  ram16Ko ram16ko_10 (
    .A(A[13:0]), .mode(mode), .sel(demultiplexer_1_out6), .clock(clock), .out(out), .Dout(Dout), .Din(Din));
  ram16Ko ram16ko_11 (
    .A(A[13:0]), .mode(mode), .sel(demultiplexer_1_out10), .clock(clock), .out(out), .Dout(Dout), .Din(Din));
  ram16Ko ram16ko_12 (
    .A(A[13:0]), .mode(mode), .sel(demultiplexer_1_out14), .clock(clock), .out(out), .Dout(Dout), .Din(Din));
  ram16Ko ram16ko_13 (
    .A(A[13:0]), .mode(mode), .sel(demultiplexer_1_out3), .clock(clock), .out(out), .Dout(Dout), .Din(Din));
  ram16Ko ram16ko_14 (
    .A(A[13:0]), .mode(mode), .sel(demultiplexer_1_out7), .clock(clock), .out(out), .Dout(Dout), .Din(Din));
  ram16Ko ram16ko_15 (
    .A(A[13:0]), .mode(mode), .sel(demultiplexer_1_out11), .clock(clock), .out(out), .Dout(Dout), .Din(Din));
  ram16Ko ram16ko_16 (
    .A(A[13:0]), .mode(mode), .sel(demultiplexer_1_out15), .clock(clock), .out(out), .Dout(Dout), .Din(Din));
endmodule

module ram4Mo (
  input  [21:0] A,
  input  [1:0] mode,
  input  [31:0] Din,
  input  sel,
  input  clock,
  input  out,
  output [31:0] Dout
);

  wire demultiplexer_1_out0, demultiplexer_1_out1, demultiplexer_1_out2, demultiplexer_1_out3,
       demultiplexer_1_out4, demultiplexer_1_out5, demultiplexer_1_out6, demultiplexer_1_out7,
       demultiplexer_1_out8, demultiplexer_1_out9, demultiplexer_1_out10, demultiplexer_1_out11,
       demultiplexer_1_out12, demultiplexer_1_out13, demultiplexer_1_out14, demultiplexer_1_out15;

  Demultiplexer #(.select(4), .enable("false")) demultiplexer_1 (
    .out0(demultiplexer_1_out0), .out1(demultiplexer_1_out1), .out2(demultiplexer_1_out2),
    .out3(demultiplexer_1_out3), .out4(demultiplexer_1_out4), .out5(demultiplexer_1_out5),
    .out6(demultiplexer_1_out6), .out7(demultiplexer_1_out7), .out8(demultiplexer_1_out8),
    .out9(demultiplexer_1_out9), .out10(demultiplexer_1_out10), .out11(demultiplexer_1_out11),
    .out12(demultiplexer_1_out12), .out13(demultiplexer_1_out13), .out14(demultiplexer_1_out14),
    .out15(demultiplexer_1_out15), .in(sel), .sel(A[21:18]));
  ram256Ko ram256ko_1 (
    .A(A[17:0]), .mode(mode), .sel(demultiplexer_1_out0), .clock(clock), .out(out), .Dout(Dout), .Din(Din));
  ram256Ko ram256ko_2 (
    .A(A[17:0]), .mode(mode), .sel(demultiplexer_1_out4), .clock(clock), .out(out), .Dout(Dout), .Din(Din));
  ram256Ko ram256ko_3 (
    .A(A[17:0]), .mode(mode), .sel(demultiplexer_1_out8), .clock(clock), .out(out), .Dout(Dout), .Din(Din));
  ram256Ko ram256ko_4 (
    .A(A[17:0]), .mode(mode), .sel(demultiplexer_1_out12), .clock(clock), .out(out), .Dout(Dout), .Din(Din));
  ram256Ko ram256ko_5 (
    .A(A[17:0]), .mode(mode), .sel(demultiplexer_1_out1), .clock(clock), .out(out), .Dout(Dout), .Din(Din));
  ram256Ko ram256ko_6 (
    .A(A[17:0]), .mode(mode), .sel(demultiplexer_1_out5), .clock(clock), .out(out), .Dout(Dout), .Din(Din));
  ram256Ko ram256ko_7 (
    .A(A[17:0]), .mode(mode), .sel(demultiplexer_1_out9), .clock(clock), .out(out), .Dout(Dout), .Din(Din));
  ram256Ko ram256ko_8 (
    .A(A[17:0]), .mode(mode), .sel(demultiplexer_1_out13), .clock(clock), .out(out), .Dout(Dout), .Din(Din));
  ram256Ko ram256ko_9 (
    .A(A[17:0]), .mode(mode), .sel(demultiplexer_1_out2), .clock(clock), .out(out), .Dout(Dout), .Din(Din));
  ram256Ko ram256ko_10 (
    .A(A[17:0]), .mode(mode), .sel(demultiplexer_1_out6), .clock(clock), .out(out), .Dout(Dout), .Din(Din));
  ram256Ko ram256ko_11 (
    .A(A[17:0]), .mode(mode), .sel(demultiplexer_1_out10), .clock(clock), .out(out), .Dout(Dout), .Din(Din));
  ram256Ko ram256ko_12 (
    .A(A[17:0]), .mode(mode), .sel(demultiplexer_1_out14), .clock(clock), .out(out), .Dout(Dout), .Din(Din));
  ram256Ko ram256ko_13 (
    .A(A[17:0]), .mode(mode), .sel(demultiplexer_1_out3), .clock(clock), .out(out), .Dout(Dout), .Din(Din));
  ram256Ko ram256ko_14 (
    .A(A[17:0]), .mode(mode), .sel(demultiplexer_1_out7), .clock(clock), .out(out), .Dout(Dout), .Din(Din));
  ram256Ko ram256ko_15 (
    .A(A[17:0]), .mode(mode), .sel(demultiplexer_1_out11), .clock(clock), .out(out), .Dout(Dout), .Din(Din));
  ram256Ko ram256ko_16 (
    .A(A[17:0]), .mode(mode), .sel(demultiplexer_1_out15), .clock(clock), .out(out), .Dout(Dout), .Din(Din));
endmodule
