// Logisim project mips32_multi.circ as structural Verilog: 12 circuits, main circuit MIPS32
module MIPS32 (
  input  Reset
);

  wire Clock_out, comparator_1_eq, comparator_2_eq, comparator_3_eq, cpu_1_read, cpu_1_write,
       keyboard_1_avail, keyboard_controler_1_int, keyboard_controler_1_read_enable;
  wire [6:0] keyboard_1_data;
  wire [31:0] cpu_1_address, cpu_1_data_out, ram_1_mem_data;

  CPU cpu_1 (
    .Int(keyboard_controler_1_int), .Reset(Reset), .Clock(Clock_out), .Read(cpu_1_read), .Write(cpu_1_write),
    .Address(cpu_1_address), .Data_in(ram_1_mem_data), .Data_out(cpu_1_data_out));
  Clock Clock (.out(Clock_out));
  Comparator #(.width(32)) comparator_1 (.a(cpu_1_address), .b(32'hfffffffd), .eq(comparator_1_eq));  // open: gt, lt
  Comparator #(.width(10), .mode("unsigned")) comparator_2 (
    .a(cpu_1_address[31:22]), .b({10{1'b0}}), .eq(comparator_2_eq));  // open: gt, lt
  TTY #(.rows(16)) tty_1 (.data(cpu_1_data_out[6:0]), .clk(Clock_out), .we(comparator_1_eq), .clr(Reset));
  Keyboard keyboard_1 (
    .clk(Clock_out), .re(keyboard_controler_1_read_enable), .clr(Reset), .avail(keyboard_1_avail),
    .data(keyboard_1_data));
  ram ram_1 (
    .Address(cpu_1_address[21:0]), .Write_data(cpu_1_data_out), .Mem_read(cpu_1_read),
    .Mem_write(cpu_1_write), .Sel(comparator_2_eq), .Clock(Clock_out), .Mem_data(ram_1_mem_data));
  Comparator #(.width(31)) comparator_3 (
    .a(cpu_1_address[31:1]), .b({31{1'b1}}), .eq(comparator_3_eq));  // open: gt, lt
  Keyboard_controler keyboard_controler_1 (
    .Read_enable(keyboard_controler_1_read_enable), .Din(cpu_1_data_out), .Available(keyboard_1_avail),
    .Ascii_in(keyboard_1_data), .A0(cpu_1_address[0]), .Read(cpu_1_read), .Write(cpu_1_write),
    .Clock(Clock_out), .Sel(comparator_3_eq), .Reset(Reset), .Ascii_out___status___control(ram_1_mem_data),
    .Int(keyboard_controler_1_int));

  // Notes on the sheet:
  //   Din
  //   CPU
  //   Dout
  //   RD
  //   @
  //   WR
  //   RAM
  //   Keyboard
  //   Keyboard controler
endmodule

module Processing_unit (
  input  [1:0] ALUOp,
  input  PCWriteCond,
  input  PCWrite,
  input  IRWrite,
  input  [2:0] PCSource,
  input  [31:0] Data_in,
  input  ALUSrcA,
  input  RegDst,
  input  RegWrite,
  input  [1:0] RegSrc,
  input  UM,
  input  EXL,
  input  [1:0] ALUSrcB,
  input  IorD,
  input  Set_EXL,
  input  Reset_EXL,
  input  [1:0] C0WriteReg,
  input  C0ReadReg,
  input  [2:0] C0Src,
  input  C0Write,
  input  Clock,
  input  Init,
  output [31:0] Instruction,
  output [31:0] Address,
  output Overflow,
  output [31:0] Data_out,
  output Bad,
  output [31:0] Status
);

  wire alu_1_zero, and_1_out, and_2_out, not_1_out, or_1_out, undriven_2;
  wire [2:0] alu_control_1_operation;
  wire [3:0] register32_1_dout_2;
  wire [4:0] instruction_register_1_instruction__15_0_2, instruction_register_1_instruction__20_16,
       instruction_register_1_instruction__25_21, multiplexer_3_out, multiplexer_4_out, multiplexer_5_out;
  wire [5:0] undriven;
  wire [10:0] instruction_register_1_instruction__15_0;
  wire [27:0] register32_1_dout;
  wire [31:0] address_translation_1_physical_address, alu_1_result, coprocessor0registerfile_1_base,
       coprocessor0registerfile_1_limit, coprocessor0registerfile_1_read_data, multiplexer_1_out,
       multiplexer_2_out, multiplexer_6_out, multiplexer_7_out, multiplexer_8_out, multiplexer_9_out,
       register_2_q, register_3_q, register_4_q, register_6_q, registerfile32_1_read_data_1,
       registerfile32_1_read_data_2, shift_left_2_1_out, shift_left_2_2_out, sign_extend_1_out;

  Register32 register32_1 (
    .Din(multiplexer_9_out), .Load(or_1_out), .Clock(Clock), .Clear(Init),
    .Dout({register32_1_dout_2, register32_1_dout}));
  Multiplexer #(.width(32), .enable("false")) multiplexer_1 (
    .in0({register32_1_dout_2, register32_1_dout}), .in1(register_6_q), .out(multiplexer_1_out), .sel(IorD));
  and and_1 (and_1_out, alu_1_zero, PCWriteCond);
  or or_1 (or_1_out, and_1_out, PCWrite);
  not not_1 (not_1_out, EXL);
  and and_2 (and_2_out, UM, not_1_out);
  Register #(.width(32)) register_1 (
    .D(address_translation_1_physical_address), .Q(Address), .clk(Clock));  // open: en, clr
  Address_translation address_translation_1 (
    .Virtual_address(multiplexer_1_out), .Base(coprocessor0registerfile_1_base),
    .Limit(coprocessor0registerfile_1_limit), .UM(and_2_out),
    .Physical_address(address_translation_1_physical_address), .Bad_address(Bad));
  Multiplexer #(.select(3), .width(32), .enable("false")) multiplexer_2 (
    .in0({32{1'b0}}), .in1(32'h10), .in2(32'h14), .in3(32'h20), .in4(32'h28), .in5(32'h30), .in6(Data_out),
    .in7({register32_1_dout_2, register32_1_dout}), .out(multiplexer_2_out), .sel(C0Src));
  Multiplexer #(.select(2), .width(5), .enable("false")) multiplexer_3 (
    .in0(instruction_register_1_instruction__15_0_2), .in1(5'b01101), .in2(5'b01110), .in3(5'b01110),
    .out(multiplexer_3_out), .sel(C0WriteReg));
  Instruction_register instruction_register_1 (
    .Din(Data_in), .Load(IRWrite), .Clock(Clock), .Instruction(Instruction),
    .Instruction__25_21(instruction_register_1_instruction__25_21),
    .Instruction__20_16(instruction_register_1_instruction__20_16),
    .Instruction__15_0({instruction_register_1_instruction__15_0_2, instruction_register_1_instruction__15_0}));  // open: Instruction__31_26
  Register #(.width(32)) register_2 (.D(Data_in), .Q(register_2_q), .clk(Clock));  // open: en, clr
  Coprocessor0RegisterFile coprocessor0registerfile_1 (
    .Read_register_number(multiplexer_4_out), .Write_register_number(multiplexer_3_out),
    .Write_data(multiplexer_2_out), .Set_EXL(Set_EXL), .Reset_EXL(Reset_EXL), .Write(C0Write), .Clock(Clock),
    .Init(Init), .Read_data(coprocessor0registerfile_1_read_data), .Status(Status),
    .Base(coprocessor0registerfile_1_base), .Limit(coprocessor0registerfile_1_limit));
  Multiplexer #(.width(5), .enable("false")) multiplexer_4 (
    .in0(instruction_register_1_instruction__20_16), .in1(5'b01110), .out(multiplexer_4_out), .sel(C0ReadReg));
  Multiplexer #(.width(5), .enable("false")) multiplexer_5 (
    .in0(instruction_register_1_instruction__20_16), .in1(instruction_register_1_instruction__15_0_2),
    .out(multiplexer_5_out), .sel(RegDst));
  Multiplexer #(.select(2), .width(32), .enable("false")) multiplexer_6 (
    .in0(register_6_q), .in1(register_2_q), .in2(register_3_q), .in3(register_3_q), .out(multiplexer_6_out),
    .sel(RegSrc));
  Sign_extend sign_extend_1 (
    .In({instruction_register_1_instruction__15_0_2, instruction_register_1_instruction__15_0}),
    .Out(sign_extend_1_out));
  Register #(.width(32)) register_3 (
    .D(coprocessor0registerfile_1_read_data), .Q(register_3_q), .clk(Clock));  // open: en, clr
  RegisterFile32 registerfile32_1 (
    .Read_register_number_1(instruction_register_1_instruction__25_21),
    .Read_register_number_2(instruction_register_1_instruction__20_16), .Write_register(multiplexer_5_out),
    .Write_data(multiplexer_6_out), .Write(RegWrite), .Clock(Clock),
    .Read_data_1(registerfile32_1_read_data_1), .Read_data_2(registerfile32_1_read_data_2));
  Shift_left_2 shift_left_2_1 (
    .In({undriven, instruction_register_1_instruction__25_21, instruction_register_1_instruction__20_16, instruction_register_1_instruction__15_0_2, instruction_register_1_instruction__15_0}),
    .Out(shift_left_2_1_out));
  Shift_left_2 shift_left_2_2 (.In(sign_extend_1_out), .Out(shift_left_2_2_out));
  Register #(.width(32)) register_4 (.D(registerfile32_1_read_data_1), .Q(register_4_q), .clk(Clock));  // open: en, clr
  Register #(.width(32)) register_5 (.D(registerfile32_1_read_data_2), .Q(Data_out), .clk(Clock));  // open: en, clr
  ALU_control alu_control_1 (
    .F(instruction_register_1_instruction__15_0[5:0]), .ALUOp(ALUOp), .Operation(alu_control_1_operation));
  Multiplexer #(.width(32), .enable("false")) multiplexer_7 (
    .in0({register32_1_dout_2, register32_1_dout}), .in1(register_4_q), .out(multiplexer_7_out), .sel(ALUSrcA));
  Multiplexer #(.select(2), .width(32), .enable("false")) multiplexer_8 (
    .in0(Data_out), .in1(32'h4), .in2(sign_extend_1_out), .in3(shift_left_2_2_out), .out(multiplexer_8_out),
    .sel(ALUSrcB));
  ALU alu_1 (
    .A(multiplexer_7_out), .B(multiplexer_8_out), .Zero(alu_1_zero), .Result(alu_1_result),
    .Overflow(Overflow), .AInvert(1'b0), .BNegate(alu_control_1_operation[2]),
    .Operation(alu_control_1_operation[1:0]));  // open: Carry_out
  Register #(.width(32)) register_6 (.D(alu_1_result), .Q(register_6_q), .clk(Clock), .clr(undriven_2));  // open: en
  Multiplexer #(.select(3), .width(32), .enable("false")) multiplexer_9 (
    .in0(alu_1_result), .in1(register_6_q), .in2({register32_1_dout_2, shift_left_2_1_out[27:0]}),
    .in3(32'h4), .in4(coprocessor0registerfile_1_read_data), .in5(coprocessor0registerfile_1_read_data),
    .in6(coprocessor0registerfile_1_read_data), .in7(coprocessor0registerfile_1_read_data),
    .out(multiplexer_9_out), .sel(PCSource));

  // Notes on the sheet:
  //   PC
  //   Translated  @
  //   Physical address
  //   Limit
  //   Base
  //   Address translation
  //   Zero
  //   Write reg n
  //   Coprocessor 0 registers
  //   Instruction register
  //   Memory data register
  //   Write data
  //   [15-0]
  //   Read rg n
  //   [25-21]
  //   [20-16]
  //   [15-11]
  //   Read data
  //   Sign extend
  //   C
  //   Instruction [25-0]
  //   Register file
  //   Shift left 2
  //   Instruction [5-0]
  //   Shift left 2
  //   A
  //   B
  //   ALU control
  //   Jump @
  //   PC [31-28]
  //   ALU
  //   ALUOut
  //   PC+4
  //   EPC
endmodule

module Control (
  input  [31:0] Instruction,
  input  Int,
  input  IE,
  input  EXL,
  input  Bad,
  input  UM,
  input  Overflow,
  input  Clock,
  input  Init,
  output [1:0] ALUOp,
  output ALUSrcA,
  output [1:0] ALUSrcB,
  output RegDst,
  output [1:0] RegSrc,
  output RegWrite,
  output IorD,
  output Write,
  output Read,
  output IRWrite,
  output [2:0] PCSrc,
  output PCWrite,
  output PCWriteCond,
  output C0ReadReg,
  output [1:0] C0WriteReg,
  output C0Write,
  output [2:0] C0Src,
  output Set_EXL,
  output Reset_EXL
);

  wire not_1_out, not_2_out, not_3_out, not_4_out;
  wire [1:0] rom_1_data;
  wire [2:0] rom_1_data_2;
  wire [4:0] adder_1_out, dispatch_i_1_address, dispatch_ii_1_address, dispatch_iii_1_address,
       multiplexer_1_out, multiplexer_3_out, register_1_q, undriven, undriven_2;
  wire [5:0] controlled_buffer_1_out, multiplexer_2_out;
  wire [5:5] and_1_out, and_2_out, and_3_out, dispatch_iv_1_bad_privilege;

  not not_1 (not_1_out, EXL);
  and and_1 (and_1_out[5], Bad, not_2_out);
  not not_2 (not_2_out, EXL);
  Dispatch_IV dispatch_iv_1 (
    .Instruction(Instruction), .UM(UM), .EXL(EXL), .Bad_privilege(dispatch_iv_1_bad_privilege[5]));
  and and_2 (and_2_out[5], Overflow, not_3_out);
  not not_3 (not_3_out, EXL);
  and and_3 (and_3_out[5], Int, IE, not_1_out);
  Dispatch_III dispatch_iii_1 (.Instruction(Instruction), .Address(dispatch_iii_1_address));
  Dispatch_I dispatch_i_1 (.Instruction(Instruction), .Address(dispatch_i_1_address));
  Dispatch_II dispatch_ii_1 (.Instruction(Instruction), .Address(dispatch_ii_1_address));
  Adder #(.width(5)) adder_1 (.a(register_1_q), .b(5'b00001), .out(adder_1_out), .cin(1'b0));  // open: cout
  assign controlled_buffer_1_out = and_3_out[5] ? {and_3_out[5], 5'b10001} : 6'bz;  // Controlled_Buffer controlled_buffer_1
  not not_4 (not_4_out, and_3_out[5]);
  Multiplexer #(.select(2), .width(5), .enable("false")) multiplexer_1 (
    .in0({5{1'b0}}), .in1(dispatch_i_1_address), .in2(dispatch_ii_1_address), .in3(adder_1_out),
    .out(multiplexer_1_out), .sel(rom_1_data));
  assign controlled_buffer_1_out = not_4_out ? {and_1_out[5], 5'b10011} : 6'bz;  // Controlled_Buffer controlled_buffer_2
  Multiplexer #(.select(3), .width(6), .enable("false")) multiplexer_2 (
    .in0({1'b0, undriven}), .in1(controlled_buffer_1_out), .in2({and_1_out[5], dispatch_iii_1_address}),
    .in3({dispatch_iv_1_bad_privilege[5], 5'b10111}), .in4({and_2_out[5], 5'b11001}),
    .in5({1'b0, undriven_2}), .in6({1'b0, undriven_2}), .in7({1'b0, undriven_2}), .out(multiplexer_2_out),
    .sel(rom_1_data_2));
  Multiplexer #(.width(5), .enable("false")) multiplexer_3 (
    .in0(multiplexer_1_out), .in1(multiplexer_2_out[4:0]), .out(multiplexer_3_out), .sel(multiplexer_2_out[5]));
  Register #(.width(5)) register_1 (.D(multiplexer_3_out), .Q(register_1_q), .clk(Clock), .clr(Init));  // open: en
  ROM #(.addrWidth(5), .dataWidth(32)) rom_1 (
    .addr(register_1_q),
    .data({ALUOp, ALUSrcA, ALUSrcB, RegDst, RegSrc, RegWrite, IorD, Write, Read, IRWrite, PCSrc, PCWrite, PCWriteCond, C0ReadReg, C0WriteReg, C0Write, C0Src, Set_EXL, Reset_EXL, rom_1_data_2, rom_1_data}),
    .sel(1'b1));

  // Notes on the sheet:
  //   Seq
  //   Ex
  //   contents of rom_1 (hex, n*v repeats v):
  //   7 8188003 1800000d 30000003 40000a 100003 1800000 200000 a0000013 4800000 60014000 28000 6800000 700
  //   397c3 d80 4a020 397c3 c00 397c3 c80 397c3 d00 397c3 e00 397c3 e80
endmodule

module CPU (
  input  [31:0] Data_in,
  input  Int,
  input  Reset,
  input  Clock,
  output Read,
  output Write,
  output [31:0] Address,
  output [31:0] Data_out
);

  wire control_1_alusrca, control_1_c0readreg, control_1_c0write, control_1_iord, control_1_irwrite,
       control_1_pcwrite, control_1_pcwritecond, control_1_regdst, control_1_regwrite, control_1_reset_exl,
       control_1_set_exl, processing_unit_1_bad, processing_unit_1_overflow, split_status_1_exl,
       split_status_1_ie, split_status_1_um;
  wire [1:0] control_1_aluop, control_1_alusrcb, control_1_c0writereg, control_1_regsrc;
  wire [2:0] control_1_c0src, control_1_pcsrc;
  wire [31:0] processing_unit_1_instruction, processing_unit_1_status;

  Processing_unit processing_unit_1 (
    .Data_in(Data_in), .UM(split_status_1_um), .EXL(split_status_1_exl), .Data_out(Data_out),
    .Instruction(processing_unit_1_instruction), .IRWrite(control_1_irwrite), .Set_EXL(control_1_set_exl),
    .Reset_EXL(control_1_reset_exl), .ALUOp(control_1_aluop), .IorD(control_1_iord), .C0Src(control_1_c0src),
    .C0WriteReg(control_1_c0writereg), .C0Write(control_1_c0write), .C0ReadReg(control_1_c0readreg),
    .Clock(Clock), .RegDst(control_1_regdst), .RegSrc(control_1_regsrc), .Init(Reset),
    .RegWrite(control_1_regwrite), .ALUSrcA(control_1_alusrca), .ALUSrcB(control_1_alusrcb),
    .Overflow(processing_unit_1_overflow), .PCSource(control_1_pcsrc), .PCWriteCond(control_1_pcwritecond),
    .PCWrite(control_1_pcwrite), .Address(Address), .Bad(processing_unit_1_bad),
    .Status(processing_unit_1_status));
  Split_status split_status_1 (
    .Status(processing_unit_1_status), .IE(split_status_1_ie), .EXL(split_status_1_exl),
    .UM(split_status_1_um));
  Control control_1 (
    .Instruction(processing_unit_1_instruction), .Int(Int), .IE(split_status_1_ie), .EXL(split_status_1_exl),
    .Bad(processing_unit_1_bad), .UM(split_status_1_um), .Overflow(processing_unit_1_overflow),
    .Clock(Clock), .Init(Reset), .ALUOp(control_1_aluop), .ALUSrcA(control_1_alusrca),
    .ALUSrcB(control_1_alusrcb), .RegDst(control_1_regdst), .RegSrc(control_1_regsrc),
    .RegWrite(control_1_regwrite), .IorD(control_1_iord), .Write(Write), .Read(Read),
    .IRWrite(control_1_irwrite), .PCSrc(control_1_pcsrc), .PCWrite(control_1_pcwrite),
    .PCWriteCond(control_1_pcwritecond), .C0ReadReg(control_1_c0readreg), .C0WriteReg(control_1_c0writereg),
    .C0Write(control_1_c0write), .C0Src(control_1_c0src), .Set_EXL(control_1_set_exl),
    .Reset_EXL(control_1_reset_exl));

  // Notes on the sheet:
  //   Processing unit
  //   Control unit
endmodule

module Address_translation (
  input  UM,
  input  [31:0] Virtual_address,
  input  [31:0] Base,
  input  [31:0] Limit,
  output [31:0] Physical_address,
  output Bad_address
);

  wire comparator_1_gt;
  wire [31:0] adder_1_out;

  Adder #(.width(32)) adder_1 (.a(Virtual_address), .b(Base), .out(adder_1_out), .cin(1'b0));  // open: cout
  Comparator #(.width(32), .mode("unsigned")) comparator_1 (
    .a(adder_1_out), .b(Limit), .gt(comparator_1_gt));  // open: eq, lt
  Multiplexer #(.width(32), .enable("false")) multiplexer_1 (
    .in0(Virtual_address), .in1(adder_1_out), .out(Physical_address), .sel(UM));
  and and_1 (Bad_address, UM, comparator_1_gt);
endmodule

module Instruction_register (
  input  Load,
  input  [31:0] Din,
  input  Clock,
  output [31:0] Instruction,
  output [5:0] Instruction__31_26,
  output [4:0] Instruction__25_21,
  output [4:0] Instruction__20_16,
  output [15:0] Instruction__15_0
);

  wire [31:0] multiplexer_1_out;

  Register #(.width(32)) register_1 (.D(multiplexer_1_out), .Q(Instruction), .clk(Clock));  // open: en, clr
  Multiplexer #(.width(32), .enable("false")) multiplexer_1 (
    .in0(Instruction), .in1(Din), .out(multiplexer_1_out), .sel(Load));

  assign Instruction__15_0 = Instruction[15:0];
  assign Instruction__20_16 = Instruction[20:16];
  assign Instruction__25_21 = Instruction[25:21];
  assign Instruction__31_26 = Instruction[31:26];
endmodule

module Dispatch_I (
  input  [31:0] Instruction,
  output [4:0] Address
);

  wire and_1_out, and_2_out, and_3_out, and_4_out, and_5_out, and_6_out, and_7_out, and_8_out, and_9_out,
       and_10_out, and_11_out, and_12_out, and_13_out, and_14_out, not_1_out, not_2_out, not_3_out,
       not_4_out, not_5_out, not_6_out, not_7_out, not_8_out, not_9_out, not_10_out, not_11_out, not_12_out,
       not_13_out, not_14_out, not_15_out, not_16_out, not_17_out, not_18_out, not_19_out, not_20_out,
       not_21_out, not_22_out, not_23_out, not_24_out, not_25_out, not_26_out, not_27_out, not_28_out,
       not_29_out, not_30_out, not_31_out, not_32_out, not_33_out, not_34_out, not_35_out, not_36_out,
       not_37_out, not_38_out, not_39_out, not_40_out, not_41_out, not_42_out, not_43_out, not_44_out,
       not_45_out, not_46_out, or_1_out;

  not not_1 (not_1_out, Instruction[31]);
  not not_2 (not_2_out, Instruction[30]);
  not not_3 (not_3_out, Instruction[29]);
  and and_1 (and_1_out, not_1_out, not_2_out, not_3_out, not_4_out, not_5_out, not_6_out);
  not not_4 (not_4_out, Instruction[28]);
  not not_5 (not_5_out, Instruction[27]);
  not not_6 (not_6_out, Instruction[26]);
  not not_7 (not_7_out, Instruction[29]);
  not not_8 (not_8_out, Instruction[30]);
  not not_9 (not_9_out, and_7_out);
  and and_2 (and_2_out, and_1_out, not_9_out);
  not not_10 (not_10_out, Instruction[28]);
  and and_3 (and_3_out, Instruction[31], not_8_out, not_7_out, not_10_out, Instruction[27], Instruction[26]);
  not not_11 (not_11_out, Instruction[30]);
  not not_12 (not_12_out, Instruction[28]);
  and and_4 (and_4_out, Instruction[31], not_11_out, Instruction[29], not_12_out, Instruction[27], Instruction[26]);
  not not_13 (not_13_out, Instruction[27]);
  not not_14 (not_14_out, Instruction[31]);
  not not_15 (not_15_out, Instruction[26]);
  not not_16 (not_16_out, Instruction[29]);
  not not_17 (not_17_out, Instruction[30]);
  and and_5 (and_5_out, not_14_out, not_17_out, not_16_out, Instruction[28], not_13_out, not_15_out);
  not not_18 (not_18_out, Instruction[29]);
  not not_19 (not_19_out, Instruction[31]);
  not not_20 (not_20_out, Instruction[30]);
  not not_21 (not_21_out, Instruction[28]);
  and and_6 (and_6_out, not_19_out, not_20_out, not_18_out, not_21_out, Instruction[27], not_26_out);
  not not_22 (not_22_out, Instruction[4]);
  not not_23 (not_23_out, Instruction[5]);
  not not_24 (not_24_out, Instruction[31]);
  not not_25 (not_25_out, Instruction[29]);
  not not_26 (not_26_out, Instruction[26]);
  not not_27 (not_27_out, Instruction[0]);
  not not_28 (not_28_out, Instruction[1]);
  and and_7 (and_7_out, not_23_out, not_22_out, Instruction[3], Instruction[2], not_28_out, not_27_out);
  not not_29 (not_29_out, Instruction[27]);
  not not_30 (not_30_out, Instruction[26]);
  not not_31 (not_31_out, Instruction[28]);
  and and_8 (and_8_out, not_24_out, Instruction[30], not_25_out, not_31_out, not_29_out, not_30_out);
  not not_32 (not_32_out, Instruction[25]);
  not not_33 (not_33_out, Instruction[24]);
  and and_9 (and_9_out, and_8_out, and_10_out);
  not not_34 (not_34_out, Instruction[23]);
  not not_35 (not_35_out, Instruction[21]);
  not not_36 (not_36_out, Instruction[22]);
  and and_10 (and_10_out, not_32_out, not_33_out, not_34_out, not_36_out, not_35_out);
  and and_11 (and_11_out, and_8_out, and_12_out);
  not not_37 (not_37_out, Instruction[24]);
  not not_38 (not_38_out, Instruction[22]);
  not not_39 (not_39_out, Instruction[25]);
  not not_40 (not_40_out, Instruction[21]);
  and and_12 (and_12_out, not_39_out, not_37_out, Instruction[23], not_38_out, not_40_out);
  not not_41 (not_41_out, Instruction[28]);
  not not_42 (not_42_out, Instruction[30]);
  not not_43 (not_43_out, Instruction[29]);
  and and_13 (and_13_out, Instruction[31], not_42_out, not_43_out, not_41_out, not_45_out, not_44_out);
  not not_44 (not_44_out, Instruction[26]);
  not not_45 (not_45_out, Instruction[27]);
  and and_14 (and_14_out, and_1_out, and_7_out);
  or or_1 (or_1_out, and_2_out, and_3_out, and_4_out, and_5_out, and_6_out, and_9_out, and_11_out, and_13_out, and_14_out);
  not not_46 (not_46_out, or_1_out);
  assign Address = and_2_out ? 5'b01000 : 5'bz;  // Controlled_Buffer controlled_buffer_1
  assign Address = and_3_out ? 5'b00011 : 5'bz;  // Controlled_Buffer controlled_buffer_2
  assign Address = and_4_out ? 5'b00011 : 5'bz;  // Controlled_Buffer controlled_buffer_3
  assign Address = and_5_out ? 5'b01010 : 5'bz;  // Controlled_Buffer controlled_buffer_4
  assign Address = and_6_out ? 5'b01011 : 5'bz;  // Controlled_Buffer controlled_buffer_5
  assign Address = and_9_out ? 5'b01100 : 5'bz;  // Controlled_Buffer controlled_buffer_6
  assign Address = and_11_out ? 5'b01101 : 5'bz;  // Controlled_Buffer controlled_buffer_7
  assign Address = and_13_out ? 5'b10000 : 5'bz;  // Controlled_Buffer controlled_buffer_8
  assign Address = and_14_out ? 5'b01110 : 5'bz;  // Controlled_Buffer controlled_buffer_9
  assign Address = not_46_out ? 5'b10111 : 5'bz;  // Controlled_Buffer controlled_buffer_10

  // Notes on the sheet:
  //   R-format
  //   lw
  //   sw
  //   beq
  //   jump
  //   mfc0
  //   mtc0
  //   eret
  //   syscall
endmodule

module Dispatch_II (
  input  [31:0] Instruction,
  output [4:0] Address
);

  wire and_1_out, and_2_out, not_1_out, not_2_out, not_3_out, not_4_out, not_5_out;

  not not_1 (not_1_out, Instruction[30]);
  not not_2 (not_2_out, Instruction[29]);
  not not_3 (not_3_out, Instruction[28]);
  and and_1 (and_1_out, Instruction[31], not_1_out, not_2_out, not_3_out, Instruction[27], Instruction[26]);
  not not_4 (not_4_out, Instruction[28]);
  not not_5 (not_5_out, Instruction[30]);
  and and_2 (and_2_out, Instruction[31], not_5_out, Instruction[29], not_4_out, Instruction[27], Instruction[26]);
  assign Address = and_1_out ? 5'b00101 : 5'bz;  // Controlled_Buffer controlled_buffer_1
  assign Address = and_2_out ? 5'b00111 : 5'bz;  // Controlled_Buffer controlled_buffer_2

  // Notes on the sheet:
  //   lw
  //   sw
endmodule

module Dispatch_III (
  input  [31:0] Instruction,
  output [4:0] Address
);

  wire and_1_out, and_2_out, not_1_out, not_2_out, not_3_out, not_4_out, not_5_out;

  not not_1 (not_1_out, Instruction[30]);
  not not_2 (not_2_out, Instruction[29]);
  not not_3 (not_3_out, Instruction[28]);
  and and_1 (and_1_out, Instruction[31], not_1_out, not_2_out, not_3_out, Instruction[27], Instruction[26]);
  not not_4 (not_4_out, Instruction[28]);
  not not_5 (not_5_out, Instruction[30]);
  and and_2 (and_2_out, Instruction[31], not_5_out, Instruction[29], not_4_out, Instruction[27], Instruction[26]);
  assign Address = and_2_out ? 5'b10101 : 5'bz;  // Controlled_Buffer controlled_buffer_1
  assign Address = and_1_out ? 5'b10011 : 5'bz;  // Controlled_Buffer controlled_buffer_2

  // Notes on the sheet:
  //   lw
  //   sw
endmodule

module Dispatch_IV (
  input  [31:0] Instruction,
  input  UM,
  input  EXL,
  output Bad_privilege
);

  wire and_1_out, and_2_out, and_3_out, and_4_out, and_5_out, not_1_out, not_2_out, not_3_out, not_4_out,
       not_5_out, not_6_out, not_7_out, not_8_out, not_9_out, not_10_out, not_11_out, not_12_out, not_13_out,
       not_14_out, not_15_out, or_1_out;

  not not_1 (not_1_out, Instruction[31]);
  not not_2 (not_2_out, Instruction[27]);
  not not_3 (not_3_out, Instruction[26]);
  not not_4 (not_4_out, Instruction[29]);
  not not_5 (not_5_out, Instruction[28]);
  and and_1 (and_1_out, not_1_out, Instruction[30], not_4_out, not_5_out, not_2_out, not_3_out);
  not not_6 (not_6_out, Instruction[25]);
  and and_2 (and_2_out, and_1_out, and_3_out);
  not not_7 (not_7_out, Instruction[21]);
  not not_8 (not_8_out, Instruction[23]);
  not not_9 (not_9_out, Instruction[24]);
  not not_10 (not_10_out, Instruction[22]);
  and and_3 (and_3_out, not_6_out, not_9_out, not_8_out, not_10_out, not_7_out);
  not not_11 (not_11_out, Instruction[22]);
  not not_12 (not_12_out, Instruction[21]);
  not not_13 (not_13_out, Instruction[25]);
  not not_14 (not_14_out, Instruction[24]);
  and and_4 (and_4_out, not_13_out, not_14_out, Instruction[23], not_11_out, not_12_out);
  and and_5 (and_5_out, and_1_out, and_4_out);
  or or_1 (or_1_out, and_2_out, and_5_out);
  not not_15 (not_15_out, EXL);
  and and_6 (Bad_privilege, or_1_out, UM, not_15_out);

  // Notes on the sheet:
  //   mfc0
  //   mtc0
endmodule

module Split_status (
  input  [31:0] Status,
  output IE,
  output EXL,
  output UM
);


  assign EXL = Status[1];
  assign IE = Status[0];
  assign UM = Status[4];
endmodule

module Keyboard_controler (
  input  Available,
  input  [6:0] Ascii_in,
  input  A0,
  input  Read,
  input  Write,
  input  [31:0] Din,
  input  Clock,
  input  Sel,
  input  Reset,
  output Read_enable,
  output [31:0] Ascii_out___status___control,
  output Int
);

  wire and_1_out, and_3_out, not_1_out;
  wire [31:0] register32_1_dout;

  and and_1 (and_1_out, A0, Sel, Write);
  Register32 register32_1 (
    .Din({{30{1'b0}}, Din[1], 1'b0}), .Load(and_1_out), .Clock(Clock), .Clear(Reset), .Dout(register32_1_dout));
  not not_1 (not_1_out, A0);
  and and_2 (Read_enable, not_1_out, Sel, Read);
  and and_3 (and_3_out, A0, Sel, Read);
  assign Ascii_out___status___control = Read_enable ? {{25{1'b0}}, Ascii_in} : 32'bz;  // Controlled_Buffer controlled_buffer_1
  assign Ascii_out___status___control = and_3_out ? {register32_1_dout[31:1], Available} : 32'bz;  // Controlled_Buffer controlled_buffer_2
  and and_4 (Int, Available, register32_1_dout[1]);
endmodule
