// Logisim project ram_rom.circ as structural Verilog: 2 circuits, main circuit ram
module ram (
  input  Mem_read,
  input  Mem_write,
  input  [21:0] Address,
  input  [31:0] Write_data,
  input  Sel,
  input  Clock,
  output [31:0] Mem_data
);

  wire and_1_out, or_1_out;

  or or_1 (or_1_out, Mem_read, Mem_write);
  and and_1 (and_1_out, or_1_out, Sel);
  ram4Mo ram4mo_1 (
    .A(Address), .mode(2'b11), .sel(and_1_out), .clock(Clock), .out(Mem_read), .Dout(Mem_data),
    .Din(Write_data));
endmodule

module rom (
  input  [21:0] Address,
  input  Sel,
  output [31:0] Mem_data
);

  ram4Mo ram4mo_1 (.A(Address), .mode(2'b11), .sel(Sel), .out(1'b1), .Dout(Mem_data));  // open: clock, Din
endmodule
