// Logisim project urisc.circ as structural Verilog: 7 circuits, main circuit register10
module register10 (
  input  load,
  input  [9:0] D,
  input  clock,
  input  clr,
  output [9:0] Q
);

  wire [9:0] multiplexer_1_out;

  Multiplexer #(.width(10), .enable("false")) multiplexer_1 (.in0(Q), .in1(D), .out(multiplexer_1_out), .sel(load));
  Register #(.width(10)) register_1 (.D(multiplexer_1_out), .Q(Q), .clk(clock), .clr(clr));  // open: en
endmodule

module register30 (
  input  load,
  input  [29:0] D,
  input  clock,
  input  clr,
  output [29:0] Q
);

  wire [29:0] multiplexer_1_out;

  Multiplexer #(.width(30), .enable("false")) multiplexer_1 (.in0(Q), .in1(D), .out(multiplexer_1_out), .sel(load));
  Register #(.width(30)) register_1 (.D(multiplexer_1_out), .Q(Q), .clk(clock), .clr(clr));  // open: en
endmodule

module counter (
  input  clk,
  input  clr,
  output s0,
  output s1,
  output s2,
  output s3
);

  D_Flip_Flop d_ff_1 (.clk(clk), .D(s3), .Q(s0), .preset(clr));  // open: Qn, en, reset
  D_Flip_Flop d_ff_2 (.clk(clk), .D(s0), .Q(s1), .reset(clr));  // open: Qn, preset, en
  D_Flip_Flop d_ff_3 (.clk(clk), .D(s1), .Q(s2), .reset(clr));  // open: Qn, preset, en
  D_Flip_Flop d_ff_4 (.clk(clk), .D(s2), .Q(s3), .reset(clr));  // open: Qn, preset, en
endmodule

module pc (
  input  load,
  input  inc,
  input  [9:0] D,
  input  clk,
  input  clr,
  output [9:0] Q
);

  wire or_1_out;
  wire [9:0] adder_1_out, multiplexer_1_out;

  Adder #(.width(10)) adder_1 (.a(Q), .b(10'h1), .out(adder_1_out), .cin(1'b0));  // open: cout
  Multiplexer #(.width(10), .enable("false")) multiplexer_1 (
    .in0(adder_1_out), .in1(D), .out(multiplexer_1_out), .sel(load));
  or or_1 (or_1_out, load, inc);
  register10 register10_1 (.D(multiplexer_1_out), .load(or_1_out), .clock(clk), .clr(clr), .Q(Q));
endmodule

module memory (
  input  RD,
  input  WR,
  input  [9:0] A,
  input  [29:0] Din,
  input  clk,
  input  clr,
  output [29:0] Dout
);

  wire or_1_out;
  wire [29:0] ram_1_data;

  or or_1 (or_1_out, RD, WR);
  RAM #(.addrWidth(10), .dataWidth(30)) ram_1 (
    .addr(A), .data(ram_1_data), .sel(or_1_out), .clk(clk), .ld(RD), .clr(clr));
  assign ram_1_data = WR ? Din : 30'bz;  // Controlled_Buffer controlled_buffer_1
  assign Dout = RD ? ram_1_data : 30'bz;  // Controlled_Buffer controlled_buffer_2
endmodule

module subtractor (
  input  [29:0] A,
  input  [29:0] B,
  output [29:0] A_B,
  output neg
);

  Subtractor #(.width(30)) subtractor_1 (.a(A), .b(B), .out(A_B), .bin(1'b0));  // open: bout

  assign neg = A_B[29];
endmodule

module urisc (
  input  reset
);

  wire and_1_out, clock_out, counter_1_s0, counter_1_s1, counter_1_s2, counter_1_s3, or_1_out, or_2_out,
       subtractor_1_neg;
  wire [9:0] controlled_buffer_1_out, register10_1_q;
  wire [29:0] memory_1_dout, register30_1_q, register30_2_q, register30_3_q, subtractor_1_a_b;

  register30 register30_1 (.D(memory_1_dout), .load(counter_1_s0), .clock(clock_out), .Q(register30_1_q));  // open: clr
  register30 register30_2 (.D(memory_1_dout), .load(counter_1_s1), .clock(clock_out), .Q(register30_2_q));  // open: clr
  register30 register30_3 (.D(memory_1_dout), .load(counter_1_s2), .clock(clock_out), .Q(register30_3_q));  // open: clr
  counter counter_1 (
    .clk(clock_out), .clr(reset), .s0(counter_1_s0), .s1(counter_1_s1), .s2(counter_1_s2), .s3(counter_1_s3));
  subtractor subtractor_1 (.A(register30_2_q), .B(register30_3_q), .neg(subtractor_1_neg), .A_B(subtractor_1_a_b));
  and and_1 (and_1_out, counter_1_s3, subtractor_1_neg);
  register10 register10_1 (
    .D(register30_1_q[9:0]), .load(and_1_out), .clock(clock_out), .clr(reset), .Q(register10_1_q));
  Clock clock (.out(clock_out));
  or or_1 (or_1_out, counter_1_s1, counter_1_s3);
  assign controlled_buffer_1_out = counter_1_s0 ? register10_1_q : 10'bz;  // Controlled_Buffer controlled_buffer_1
  assign controlled_buffer_1_out = counter_1_s2 ? register30_1_q[19:10] : 10'bz;  // Controlled_Buffer controlled_buffer_2
  assign controlled_buffer_1_out = or_1_out ? register30_1_q[29:20] : 10'bz;  // Controlled_Buffer controlled_buffer_3
  or or_2 (or_2_out, counter_1_s2, counter_1_s1, counter_1_s0);
  memory memory_1 (
    .A(controlled_buffer_1_out), .Din(subtractor_1_a_b), .RD(or_2_out), .WR(counter_1_s3), .clk(clock_out),
    .Dout(memory_1_dout));  // open: clr
  // Probe on memory_1_dout

  // Notes on the sheet:
  //   IR
  //   COUNTER
  //   OP1
  //   OP2
  //   PC
  //   RAM
endmodule
